// Logisim project 实验5-CS2001-23345-XXX.circ as structural Verilog: 14 circuits, main circuit 四位二进制可逆计数器
module \四位二进制可逆计数器  (
  input  D,
  input  C,
  input  B,
  input  CPu,
  input  CPd,
  input  A,
  input  nLD,
  input  CLR,
  output QD,
  output QC,
  output QB,
  output QA
);

  wire and_1_out, and_2_out, and_3_out, and_4_out, and_5_out, and_6_out, and_7_out, and_8_out, and_9_out,
       and_10_out, and_11_out, and_12_out, and_13_out, and_14_out, d_ff_1_qn, d_ff_2_qn, d_ff_3_qn,
       d_ff_4_qn, not_1_out, not_2_out, not_3_out, not_4_out, not_5_out, or_1_out, or_2_out, or_3_out,
       or_4_out, or_5_out, or_6_out, or_7_out, or_8_out;

  and and_1 (and_1_out, CPu, QA, QB, QC);
  and and_2 (and_2_out, CPd, d_ff_3_qn, d_ff_2_qn, d_ff_4_qn);
  and and_3 (and_3_out, CPu, QA, QB);
  and and_4 (and_4_out, CPd, d_ff_3_qn, d_ff_4_qn);
  and and_5 (and_5_out, CPu, QA);
  and and_6 (and_6_out, CPd, d_ff_4_qn);
  or or_1 (or_1_out, and_1_out, and_2_out);
  or or_2 (or_2_out, and_3_out, and_4_out);
  or or_3 (or_3_out, and_5_out, and_6_out);
  or or_4 (or_4_out, CPu, CPd);
  D_Flip_Flop #(.trigger("falling"), .Pre_Clr_Positions("LEGACY"), .NegatePresetClear("false"), .enable("true"), .NewFFLayout("false")) d_ff_1 (
    .clk(or_1_out), .D(d_ff_1_qn), .Q(QD), .Qn(d_ff_1_qn), .preset(and_8_out), .en(nLD), .reset(or_5_out));
  or or_5 (or_5_out, and_7_out, CLR);
  D_Flip_Flop #(.trigger("falling"), .Pre_Clr_Positions("LEGACY"), .NegatePresetClear("false"), .enable("true"), .NewFFLayout("false")) d_ff_2 (
    .clk(or_2_out), .D(d_ff_2_qn), .Q(QC), .Qn(d_ff_2_qn), .preset(and_10_out), .en(nLD), .reset(or_6_out));
  or or_6 (or_6_out, and_9_out, CLR);
  D_Flip_Flop #(.trigger("falling"), .Pre_Clr_Positions("LEGACY"), .NegatePresetClear("false"), .enable("true"), .NewFFLayout("false")) d_ff_3 (
    .clk(or_3_out), .D(d_ff_3_qn), .Q(QB), .Qn(d_ff_3_qn), .preset(and_12_out), .en(nLD), .reset(or_7_out));
  or or_7 (or_7_out, and_11_out, CLR);
  D_Flip_Flop #(.trigger("falling"), .Pre_Clr_Positions("LEGACY"), .NegatePresetClear("false"), .enable("true"), .NewFFLayout("false")) d_ff_4 (
    .clk(or_4_out), .D(d_ff_4_qn), .Q(QA), .Qn(d_ff_4_qn), .preset(and_14_out), .en(nLD), .reset(or_8_out));
  or or_8 (or_8_out, and_13_out, CLR);
  and and_7 (and_7_out, not_2_out, not_1_out);
  and and_8 (and_8_out, D, not_1_out);
  and and_9 (and_9_out, not_3_out, not_1_out);
  and and_10 (and_10_out, C, not_1_out);
  and and_11 (and_11_out, not_4_out, not_1_out);
  and and_12 (and_12_out, B, not_1_out);
  and and_13 (and_13_out, not_5_out, not_1_out);
  and and_14 (and_14_out, A, not_1_out);
  not not_1 (not_1_out, nLD);
  not not_2 (not_2_out, D);
  not not_3 (not_3_out, C);
  not not_4 (not_4_out, B);
  not not_5 (not_5_out, A);
endmodule

module \六十进制计数器  (
  input  CPU,
  input  CPD,
  input  Adj,
  input  CLR,
  output Q0d,
  output Q0c,
  output Q0b,
  output Q0a,
  output nQcc,
  output Q1d,
  output Q1c,
  output Q1b,
  output Q1a
);

  wire and_1_out, and_2_out, and_3_out, and_4_out, not_1_out, not_2_out, not_3_out, not_4_out, or_1_out,
       or_2_out, or_4_out, or_5_out;

  and and_1 (and_1_out, or_1_out, CPD, Adj);
  or or_1 (or_1_out, Q0d, Q0c, Q0b, Q0a, or_4_out);
  or or_2 (or_2_out, and_3_out, CLR);
  not not_1 (not_1_out, Q0c);
  not not_2 (not_2_out, Q0a);
  \四位二进制可逆计数器  \u_四位二进制可逆计数器_1  (
    .CPu(CPU), .CPd(and_1_out), .nLD(not_3_out), .CLR(or_2_out), .QD(Q0d), .D(1'b1), .QC(Q0c), .C(1'b0),
    .QB(Q0b), .B(1'b0), .QA(Q0a), .A(1'b1));
  and and_2 (and_2_out, Q0d, Q0c, Q0b, Q0a);
  and and_3 (and_3_out, Q0d, not_1_out, Q0b, not_2_out);
  not not_3 (not_3_out, and_2_out);
  or or_3 (nQcc, Adj, not_4_out);
  not not_4 (not_4_out, and_4_out);
  or or_4 (or_4_out, Q1d, Q1c, Q1b, Q1a);
  and and_4 (and_4_out, Q1c, Q1b);
  or or_5 (or_5_out, and_4_out, CLR);
  \四位二进制可逆计数器  \u_四位二进制可逆计数器_2  (
    .CPu(and_3_out), .CPd(and_2_out), .nLD(1'b1), .CLR(or_5_out), .QD(Q1d), .D(1'b0), .QC(Q1c), .C(1'b0),
    .QB(Q1b), .B(1'b0), .QA(Q1a), .A(1'b0));
endmodule

module \六十进制计数器测试电路  (
  input  in_1,
  input  in_2,
  output out_3
);

  wire button_1_out, button_2_out;
  wire [3:0] \六十进制计数器_1_q0a , \六十进制计数器_1_q1a ;

  Button button_1 (.out(button_1_out));
  Button button_2 (.out(button_2_out));
  Hex_Digit_Display hex_digit_display_1 (.value(\六十进制计数器_1_q1a ));  // open: dp
  \六十进制计数器  \u_六十进制计数器_1  (
    .CPU(button_1_out), .CPD(button_2_out), .Adj(in_1), .CLR(in_2), .Q0d(\六十进制计数器_1_q0a [3]),
    .Q0c(\六十进制计数器_1_q0a [2]), .Q0b(\六十进制计数器_1_q0a [1]), .Q0a(\六十进制计数器_1_q0a [0]), .nQcc(out_3),
    .Q1d(\六十进制计数器_1_q1a [3]), .Q1c(\六十进制计数器_1_q1a [2]), .Q1b(\六十进制计数器_1_q1a [1]), .Q1a(\六十进制计数器_1_q1a [0]));
  Hex_Digit_Display hex_digit_display_2 (.value(\六十进制计数器_1_q0a ));  // open: dp
endmodule

module \十二进制计数器或二十四进制的计数器电路  (
  input  in_1,
  input  in_2,
  input  in_3,
  input  in_4,
  output out_5,
  output out_6,
  output out_7,
  output out_8,
  output out_9,
  output out_10,
  output out_11,
  output out_12,
  output out_13
);

  wire and_1_out, or_1_out;

  \六十进制计数器  \u_六十进制计数器_1  (
    .CPU(in_1), .CPD(in_3), .Adj(in_2), .CLR(or_1_out), .Q0d(out_9), .Q0c(out_10), .Q0b(out_11),
    .Q0a(out_12), .Q1d(out_5), .Q1c(out_6), .Q1b(out_7), .Q1a(out_8));  // open: nQcc
  or or_1 (or_1_out, and_1_out, in_4);
  and and_1 (and_1_out, out_7, out_10);
  not not_1 (out_13, and_1_out);
endmodule

module \十二进制计数器或二十四进制的计数器测试电路  (
  input  in_1,
  input  in_2,
  output out_3
);

  wire button_1_out, button_2_out;
  wire [3:0] \十二进制计数器或二十四进制的计数器电路_1_out_8 , \十二进制计数器或二十四进制的计数器电路_1_out_12 ;

  Hex_Digit_Display hex_digit_display_1 (.value(\十二进制计数器或二十四进制的计数器电路_1_out_8 ));  // open: dp
  Button button_1 (.out(button_1_out));
  Button button_2 (.out(button_2_out));
  Hex_Digit_Display hex_digit_display_2 (.value(\十二进制计数器或二十四进制的计数器电路_1_out_12 ));  // open: dp
  \十二进制计数器或二十四进制的计数器电路  \u_十二进制计数器或二十四进制的计数器电路_1  (
    .in_1(button_1_out), .in_2(in_1), .in_3(button_2_out), .out_13(out_3), .in_4(in_2),
    .out_5(\十二进制计数器或二十四进制的计数器电路_1_out_8 [3]), .out_6(\十二进制计数器或二十四进制的计数器电路_1_out_8 [2]),
    .out_7(\十二进制计数器或二十四进制的计数器电路_1_out_8 [1]), .out_8(\十二进制计数器或二十四进制的计数器电路_1_out_8 [0]),
    .out_9(\十二进制计数器或二十四进制的计数器电路_1_out_12 [3]), .out_10(\十二进制计数器或二十四进制的计数器电路_1_out_12 [2]),
    .out_11(\十二进制计数器或二十四进制的计数器电路_1_out_12 [1]), .out_12(\十二进制计数器或二十四进制的计数器电路_1_out_12 [0]));
endmodule

module \上下午文字显示的电路  (
  input  in_1,
  input  in_2,
  output [4:0] out_3,
  output [4:0] out_4,
  output [4:0] out_5,
  output [4:0] out_6
);

  wire not_1_out;

  and and_1 (out_3[4], in_1, in_2);
  and and_2 (out_3[0], not_1_out, in_2);
  not not_1 (not_1_out, in_1);

  assign out_3[3:1] = 3'b000;
  assign out_4 = {5{in_2}};
  assign out_5 = {out_3[4], 1'b0, in_2, 1'b0, out_3[0]};
  assign out_6 = {out_3[4], 3'b000, out_3[0]};
endmodule

module \上下午文字显示测试电路  (
  input  in_1,
  input  in_2
);

  wire [4:0] \上下午文字显示的电路_1_out_3 , \上下午文字显示的电路_1_out_4 , \上下午文字显示的电路_1_out_5 , \上下午文字显示的电路_1_out_6 ;

  DotMatrix #(.inputtype("column"), .matrixcols(4), .matrixrows(5), .persist(0), .dotshape("square")) dotmatrix_1 (
    .col0(\上下午文字显示的电路_1_out_3 ), .col1(\上下午文字显示的电路_1_out_4 ), .col2(\上下午文字显示的电路_1_out_5 ),
    .col3(\上下午文字显示的电路_1_out_6 ));
  \上下午文字显示的电路  \u_上下午文字显示的电路_1  (
    .out_3(\上下午文字显示的电路_1_out_3 ), .out_4(\上下午文字显示的电路_1_out_4 ), .out_5(\上下午文字显示的电路_1_out_5 ),
    .out_6(\上下午文字显示的电路_1_out_6 ), .in_1(in_1), .in_2(in_2));
endmodule

module \电子钟整点报时电路  (
  input  in_1,
  input  in_2,
  input  in_3,
  input  in_4,
  input  in_5,
  input  in_6,
  input  in_7,
  input  in_8,
  input  in_9,
  input  in_10,
  input  in_11,
  input  in_12,
  input  in_13,
  output out_14
);

  wire and_1_out, and_3_out, and_4_out, and_5_out, not_1_out, not_2_out, not_3_out, not_4_out, not_5_out,
       not_6_out;

  not not_1 (not_1_out, in_2);
  and and_1 (and_1_out, not_1_out, in_3, not_2_out, in_5);
  not not_2 (not_2_out, in_4);
  and and_2 (out_14, in_1, and_3_out);
  and and_3 (and_3_out, and_1_out, and_4_out, and_5_out);
  not not_3 (not_3_out, in_7);
  and and_4 (and_4_out, in_6, not_3_out, not_4_out, in_9);
  not not_4 (not_4_out, in_8);
  and and_5 (and_5_out, not_5_out, in_11, not_6_out, in_13);
  not not_5 (not_5_out, in_10);
  not not_6 (not_6_out, in_12);
endmodule

module \电子钟整点报时电路测试电路  (
  input  in_1,
  input  [3:0] in_2,
  input  [3:0] in_3,
  input  [3:0] in_4
);

  wire \电子钟整点报时电路_1_out_14 ;

  \电子钟整点报时电路  \u_电子钟整点报时电路_1  (
    .out_14(\电子钟整点报时电路_1_out_14 ), .in_2(in_2[3]), .in_3(in_2[2]), .in_4(in_2[1]), .in_5(in_2[0]),
    .in_6(in_3[3]), .in_1(in_1), .in_7(in_3[2]), .in_8(in_3[1]), .in_9(in_3[0]), .in_10(in_4[3]),
    .in_11(in_4[2]), .in_12(in_4[1]), .in_13(in_4[0]));
  LED #(.active("true")) led_1 (.in(\电子钟整点报时电路_1_out_14 ));
endmodule

module \多功能数字钟  (
  input  Set,
  input  AlarmON,
  input  CLR,
  input  AlarmAdj,
  input  CP,
  input  CPU,
  input  CPD,
  input  Adj1,
  input  Adj0,
  output [3:0] _10M,
  output [3:0] _1M,
  output [3:0] _10H,
  output [3:0] _1H,
  output [3:0] _10S,
  output [3:0] _1S,
  output out_16,
  output out_17,
  output [4:0] out_18,
  output [4:0] out_19,
  output [4:0] out_20,
  output [4:0] out_21
);

  wire and_1_out, and_2_out, and_3_out, and_4_out, and_5_out, and_6_out, and_7_out, and_8_out, and_9_out,
       and_10_out, and_11_out, and_12_out, and_13_out, and_14_out, comparator_1_eq, comparator_1_gt,
       comparator_2_eq, not_1_out, not_2_out, not_3_out, not_4_out, not_5_out, or_1_out, or_2_out, or_3_out,
       \六十进制计数器_1_nqcc , \六十进制计数器_2_nqcc , \秒脉冲产生电路_1_out_2 ;
  wire [3:0] bit_extender_3_out, bit_extender_4_out, multiplexer_5_out, multiplexer_6_out, \六十进制计数器_1_q0a ,
       \六十进制计数器_1_q1a , \六十进制计数器_2_q0a , \六十进制计数器_2_q1a , \十二进制计数器或二十四进制的计数器电路_1_out_8 ,
       \十二进制计数器或二十四进制的计数器电路_1_out_12 , \闹钟_1__1h_2 , \闹钟_1__1m_2 , \闹钟_1__10h_2 , \闹钟_1__10m_2 ;
  wire [7:0] adder_1_out, bit_extender_1_out, bit_extender_2_out, divider_1_rem, divider_2_out,
       divider_2_rem, multiplexer_9_out, multiplier_1_out;

  and and_1 (and_1_out, AlarmAdj, Adj1);
  and and_2 (and_2_out, AlarmAdj, Adj0);
  and and_3 (and_3_out, AlarmAdj, CPU);
  and and_4 (and_4_out, AlarmAdj, CPD);
  and and_5 (and_5_out, AlarmAdj, CLR);
  and and_6 (and_6_out, CLR, not_1_out);
  not not_1 (not_1_out, AlarmAdj);
  \秒脉冲产生电路  \u_秒脉冲产生电路_1  (.in_1(CP), .out_2(\秒脉冲产生电路_1_out_2 ));
  Multiplexer #(.select(1), .width(4), .disabled("Z"), .enable("false")) multiplexer_1 (
    .in0(\六十进制计数器_1_q1a ), .in1(4'b0000), .out(_10S), .sel(AlarmAdj));
  not not_2 (not_2_out, Adj1);
  Multiplexer #(.select(1), .width(4), .disabled("Z"), .enable("false")) multiplexer_2 (
    .in0(\六十进制计数器_1_q0a ), .in1(4'b0000), .out(_1S), .sel(AlarmAdj));
  \六十进制计数器  \u_六十进制计数器_1  (
    .CPU(\秒脉冲产生电路_1_out_2 ), .CPD(1'b0), .Adj(1'b0), .CLR(and_6_out), .Q0d(\六十进制计数器_1_q0a [3]),
    .Q0c(\六十进制计数器_1_q0a [2]), .Q0b(\六十进制计数器_1_q0a [1]), .Q0a(\六十进制计数器_1_q0a [0]), .nQcc(\六十进制计数器_1_nqcc ),
    .Q1d(\六十进制计数器_1_q1a [3]), .Q1c(\六十进制计数器_1_q1a [2]), .Q1b(\六十进制计数器_1_q1a [1]), .Q1a(\六十进制计数器_1_q1a [0]));
  and and_7 (and_7_out, CPU, not_1_out);
  and and_8 (and_8_out, Adj1, Adj0, not_1_out);
  and and_9 (and_9_out, CPD, not_1_out);
  and and_10 (and_10_out, and_7_out, and_8_out);
  and and_11 (and_11_out, and_8_out, and_9_out);
  not not_3 (not_3_out, \六十进制计数器_1_nqcc );
  or or_1 (or_1_out, not_3_out, and_10_out);
  \闹钟  \u_闹钟_1  (
    ._10Sec(\六十进制计数器_1_q1a ), .ON(AlarmON), ._1H(\十二进制计数器或二十四进制的计数器电路_1_out_12 ),
    ._10H(\十二进制计数器或二十四进制的计数器电路_1_out_8 ), ._1M(\六十进制计数器_2_q0a ), ._10M(\六十进制计数器_2_q1a ), .Adj1(and_1_out),
    .Adj0(and_2_out), .CPu(and_3_out), .CPd(and_4_out), .CLR(and_5_out), .out_16(out_16),
    ._10M_2(\闹钟_1__10m_2 ), ._1M_2(\闹钟_1__1m_2 ), ._10H_2(\闹钟_1__10h_2 ), ._1H_2(\闹钟_1__1h_2 ));
  \电子钟整点报时电路  \u_电子钟整点报时电路_1  (
    .out_14(out_17), .in_2(\六十进制计数器_2_q1a [3]), .in_3(\六十进制计数器_2_q1a [2]), .in_4(\六十进制计数器_2_q1a [1]),
    .in_5(\六十进制计数器_2_q1a [0]), .in_6(\六十进制计数器_2_q0a [3]), .in_1(CP), .in_7(\六十进制计数器_2_q0a [2]),
    .in_8(\六十进制计数器_2_q0a [1]), .in_9(\六十进制计数器_2_q0a [0]), .in_10(\六十进制计数器_1_q1a [3]),
    .in_11(\六十进制计数器_1_q1a [2]), .in_12(\六十进制计数器_1_q1a [1]), .in_13(\六十进制计数器_1_q1a [0]));
  Multiplexer #(.select(1), .width(4), .disabled("Z"), .enable("false")) multiplexer_3 (
    .in0(\六十进制计数器_2_q1a ), .in1(\闹钟_1__10m_2 ), .out(_10M), .sel(AlarmAdj));
  \六十进制计数器  \u_六十进制计数器_2  (
    .CPU(or_1_out), .CPD(and_11_out), .Adj(and_8_out), .CLR(and_6_out), .Q0d(\六十进制计数器_2_q0a [3]),
    .Q0c(\六十进制计数器_2_q0a [2]), .Q0b(\六十进制计数器_2_q0a [1]), .Q0a(\六十进制计数器_2_q0a [0]), .nQcc(\六十进制计数器_2_nqcc ),
    .Q1d(\六十进制计数器_2_q1a [3]), .Q1c(\六十进制计数器_2_q1a [2]), .Q1b(\六十进制计数器_2_q1a [1]), .Q1a(\六十进制计数器_2_q1a [0]));
  and and_12 (and_12_out, Adj0, not_2_out, not_1_out);
  Multiplexer #(.select(1), .width(4), .disabled("Z"), .enable("false")) multiplexer_4 (
    .in0(\六十进制计数器_2_q0a ), .in1(\闹钟_1__1m_2 ), .out(_1M), .sel(AlarmAdj));
  and and_13 (and_13_out, and_7_out, and_12_out);
  not not_4 (not_4_out, \六十进制计数器_2_nqcc );
  or or_2 (or_2_out, not_4_out, and_13_out);
  and and_14 (and_14_out, and_9_out, and_12_out);
  Multiplexer #(.select(1), .width(4), .disabled("Z"), .enable("false")) multiplexer_5 (
    .in0(\十二进制计数器或二十四进制的计数器电路_1_out_8 ), .in1(\闹钟_1__10h_2 ), .out(multiplexer_5_out), .sel(AlarmAdj));
  Multiplexer #(.select(1), .width(4), .disabled("Z"), .enable("false")) multiplexer_6 (
    .in0(\十二进制计数器或二十四进制的计数器电路_1_out_12 ), .in1(\闹钟_1__1h_2 ), .out(multiplexer_6_out), .sel(AlarmAdj));
  \十二进制计数器或二十四进制的计数器电路  \u_十二进制计数器或二十四进制的计数器电路_1  (
    .in_1(or_2_out), .in_2(and_12_out), .in_3(and_14_out), .in_4(and_6_out),
    .out_5(\十二进制计数器或二十四进制的计数器电路_1_out_8 [3]), .out_6(\十二进制计数器或二十四进制的计数器电路_1_out_8 [2]),
    .out_7(\十二进制计数器或二十四进制的计数器电路_1_out_8 [1]), .out_8(\十二进制计数器或二十四进制的计数器电路_1_out_8 [0]),
    .out_9(\十二进制计数器或二十四进制的计数器电路_1_out_12 [3]), .out_10(\十二进制计数器或二十四进制的计数器电路_1_out_12 [2]),
    .out_11(\十二进制计数器或二十四进制的计数器电路_1_out_12 [1]), .out_12(\十二进制计数器或二十四进制的计数器电路_1_out_12 [0]));  // open: out_13
  Multiplexer #(.select(1), .width(4), .disabled("Z"), .enable("false")) multiplexer_7 (
    .in0(bit_extender_3_out), .in1(multiplexer_5_out), .out(_10H), .sel(Set));
  assign bit_extender_1_out = {{4{1'b0}}, multiplexer_5_out};  // Bit_Extender bit_extender_1
  Multiplexer #(.select(1), .width(4), .disabled("Z"), .enable("false")) multiplexer_8 (
    .in0(bit_extender_4_out), .in1(multiplexer_6_out), .out(_1H), .sel(Set));
  assign bit_extender_2_out = {{4{1'b0}}, multiplexer_6_out};  // Bit_Extender bit_extender_2
  Multiplier #(.width(8)) multiplier_1 (.a(bit_extender_1_out), .b(8'ha), .out(multiplier_1_out));  // open: cin, cout
  \上下午文字显示的电路  \u_上下午文字显示的电路_1  (
    .out_3(out_18), .out_4(out_19), .out_5(out_20), .out_6(out_21), .in_1(or_3_out), .in_2(not_5_out));
  not not_5 (not_5_out, Set);
  Adder #(.width(8)) adder_1 (.a(bit_extender_2_out), .b(multiplier_1_out), .out(adder_1_out));  // open: cin, cout
  Comparator #(.width(8), .mode("twosComplement")) comparator_1 (
    .a(adder_1_out), .b(8'hc), .gt(comparator_1_gt), .eq(comparator_1_eq));  // open: lt
  Bit_Extender #(.in_width(8), .out_width(4), .\type ("zero")) bit_extender_3 (
    .in(divider_2_out), .out(bit_extender_3_out));
  Bit_Extender #(.in_width(8), .out_width(4), .\type ("zero")) bit_extender_4 (
    .in(divider_2_rem), .out(bit_extender_4_out));
  Divider #(.width(8)) divider_1 (.a(adder_1_out), .b(8'hc), .rem(divider_1_rem));  // open: out, upper
  or or_3 (or_3_out, comparator_1_eq, comparator_1_gt);
  Divider #(.width(8)) divider_2 (
    .a(multiplexer_9_out), .b(8'ha), .out(divider_2_out), .rem(divider_2_rem));  // open: upper
  Comparator #(.width(8), .mode("twosComplement")) comparator_2 (
    .a({8{1'b0}}), .b(divider_1_rem), .eq(comparator_2_eq));  // open: gt, lt
  Multiplexer #(.select(1), .width(8), .disabled("Z"), .enable("false")) multiplexer_9 (
    .in0(divider_1_rem), .in1(8'hc), .out(multiplexer_9_out), .sel(comparator_2_eq));
endmodule

module \秒脉冲产生电路  (
  input  in_1,
  output out_2
);

  wire not_1_out;

  not not_1 (not_1_out, 1'b1);
  \四位二进制可逆计数器  \u_四位二进制可逆计数器_1  (
    .CPu(in_1), .CPd(not_1_out), .nLD(1'b1), .CLR(out_2), .QD(out_2), .D(not_1_out), .C(not_1_out),
    .B(not_1_out), .A(not_1_out));  // open: QC, QB, QA
endmodule

module \多功能数字钟测试电路  (
  input  in_1,
  input  in_2,
  input  in_3,
  input  in_4,
  input  in_5
);

  wire button_1_out, button_2_out, button_3_out, clock_1_out, \多功能数字钟_1_out_16 , \多功能数字钟_1_out_17 ;
  wire [3:0] \多功能数字钟_1__1h , \多功能数字钟_1__1m , \多功能数字钟_1__1s , \多功能数字钟_1__10h , \多功能数字钟_1__10m ,
       \多功能数字钟_1__10s ;
  wire [4:0] \多功能数字钟_1_out_18 , \多功能数字钟_1_out_19 , \多功能数字钟_1_out_20 , \多功能数字钟_1_out_21 ;

  DotMatrix #(.inputtype("column"), .matrixcols(4), .matrixrows(5), .persist(0), .dotshape("square")) dotmatrix_1 (
    .col0(\多功能数字钟_1_out_18 ), .col1(\多功能数字钟_1_out_19 ), .col2(\多功能数字钟_1_out_20 ), .col3(\多功能数字钟_1_out_21 ));
  \多功能数字钟  \u_多功能数字钟_1  (
    .Set(in_5), .AlarmON(in_3), .CLR(button_3_out), .AlarmAdj(in_2), .CP(clock_1_out), .CPU(button_1_out),
    .CPD(button_2_out), .Adj1(in_1), .Adj0(in_4), .out_16(\多功能数字钟_1_out_16 ), .out_17(\多功能数字钟_1_out_17 ),
    ._10S(\多功能数字钟_1__10s ), ._1S(\多功能数字钟_1__1s ), ._10M(\多功能数字钟_1__10m ), ._1M(\多功能数字钟_1__1m ),
    ._10H(\多功能数字钟_1__10h ), ._1H(\多功能数字钟_1__1h ), .out_18(\多功能数字钟_1_out_18 ), .out_19(\多功能数字钟_1_out_19 ),
    .out_20(\多功能数字钟_1_out_20 ), .out_21(\多功能数字钟_1_out_21 ));
  Clock #(.highDuration(1), .lowDuration(1)) clock_1 (.out(clock_1_out));
  Hex_Digit_Display hex_digit_display_1 (.value(\多功能数字钟_1__10h ));  // open: dp
  Button button_1 (.out(button_1_out));
  Hex_Digit_Display hex_digit_display_2 (.value(\多功能数字钟_1__10m ));  // open: dp
  Hex_Digit_Display hex_digit_display_3 (.value(\多功能数字钟_1__1h ));  // open: dp
  Button button_2 (.out(button_2_out));
  Hex_Digit_Display hex_digit_display_4 (.value(\多功能数字钟_1__1m ));  // open: dp
  Hex_Digit_Display hex_digit_display_5 (.value(\多功能数字钟_1__1s ));  // open: dp
  Hex_Digit_Display hex_digit_display_6 (.value(\多功能数字钟_1__10s ));  // open: dp
  Button button_3 (.out(button_3_out));
  LED #(.active("true")) led_1 (.in(\多功能数字钟_1_out_16 ));
  LED #(.active("true")) led_2 (.in(\多功能数字钟_1_out_17 ));
endmodule

module \闹钟  (
  input  [3:0] _10Sec,
  input  ON,
  input  [3:0] _1H,
  input  [3:0] _10H,
  input  [3:0] _1M,
  input  [3:0] _10M,
  input  Adj1,
  input  Adj0,
  input  CPu,
  input  CPd,
  input  CLR,
  output [3:0] _10M_2,
  output [3:0] _1M_2,
  output [3:0] _10H_2,
  output [3:0] _1H_2,
  output out_16
);

  wire and_1_out, and_2_out, and_3_out, and_4_out, and_5_out, and_6_out, comparator_1_eq, comparator_2_eq,
       comparator_3_eq, comparator_4_eq, comparator_5_eq, not_1_out;

  not not_1 (not_1_out, Adj1);
  and and_1 (and_1_out, Adj1, Adj0);
  and and_2 (and_2_out, not_1_out, Adj0);
  and and_3 (and_3_out, and_1_out, CPu);
  and and_4 (and_4_out, and_1_out, CPd);
  Comparator #(.width(4), .mode("twosComplement")) comparator_1 (
    .a(_10M), .b(_10M_2), .eq(comparator_1_eq));  // open: gt, lt
  \六十进制计数器  \u_六十进制计数器_1  (
    .CPU(and_3_out), .CPD(and_4_out), .Adj(and_1_out), .CLR(CLR), .Q0d(_1M_2[3]), .Q0c(_1M_2[2]),
    .Q0b(_1M_2[1]), .Q0a(_1M_2[0]), .Q1d(_10M_2[3]), .Q1c(_10M_2[2]), .Q1b(_10M_2[1]), .Q1a(_10M_2[0]));  // open: nQcc
  Comparator #(.width(4), .mode("twosComplement")) comparator_2 (
    .a(_1M), .b(_1M_2), .eq(comparator_2_eq));  // open: gt, lt
  and and_5 (and_5_out, CPu, and_2_out);
  and and_6 (and_6_out, CPd, and_2_out);
  Comparator #(.width(4), .mode("twosComplement")) comparator_3 (
    .a(_10H), .b(_10H_2), .eq(comparator_3_eq));  // open: gt, lt
  Comparator #(.width(4), .mode("twosComplement")) comparator_4 (
    .a(_1H), .b(_1H_2), .eq(comparator_4_eq));  // open: gt, lt
  \十二进制计数器或二十四进制的计数器电路  \u_十二进制计数器或二十四进制的计数器电路_1  (
    .in_1(and_5_out), .in_2(and_2_out), .in_3(and_6_out), .in_4(CLR), .out_5(_10H_2[3]), .out_6(_10H_2[2]),
    .out_7(_10H_2[1]), .out_8(_10H_2[0]), .out_9(_1H_2[3]), .out_10(_1H_2[2]), .out_11(_1H_2[1]),
    .out_12(_1H_2[0]));  // open: out_13
  Comparator #(.width(4), .mode("twosComplement")) comparator_5 (
    .a(4'b0000), .b(_10Sec), .eq(comparator_5_eq));  // open: gt, lt
  and and_7 (out_16, comparator_5_eq, comparator_1_eq, comparator_2_eq, comparator_3_eq, comparator_4_eq, ON);
endmodule

module \闹钟测试  (
  input  in_1,
  input  in_2,
  input  in_3,
  input  in_4,
  input  [3:0] in_5,
  input  [3:0] in_6,
  input  [3:0] in_7,
  input  [3:0] in_8,
  input  [3:0] in_9
);

  wire button_1_out, button_2_out, \闹钟_1_out_16 ;
  wire [3:0] \闹钟_1__1h_2 , \闹钟_1__1m_2 , \闹钟_1__10h_2 , \闹钟_1__10m_2 ;

  Button button_1 (.out(button_1_out));
  Button button_2 (.out(button_2_out));
  Hex_Digit_Display hex_digit_display_1 (.value(\闹钟_1__10h_2 ));  // open: dp
  Hex_Digit_Display hex_digit_display_2 (.value(\闹钟_1__1h_2 ));  // open: dp
  Hex_Digit_Display hex_digit_display_3 (.value(\闹钟_1__10m_2 ));  // open: dp
  Hex_Digit_Display hex_digit_display_4 (.value(\闹钟_1__1m_2 ));  // open: dp
  \闹钟  \u_闹钟_1  (
    ._10Sec(in_9), .ON(in_1), ._1H(in_6), ._10H(in_5), ._1M(in_8), ._10M(in_7), .Adj1(in_2), .Adj0(in_3),
    .CPu(button_1_out), .CPd(button_2_out), .CLR(in_4), .out_16(\闹钟_1_out_16 ), ._10M_2(\闹钟_1__10m_2 ),
    ._1M_2(\闹钟_1__1m_2 ), ._10H_2(\闹钟_1__10h_2 ), ._1H_2(\闹钟_1__1h_2 ));
  LED #(.active("true")) led_1 (.in(\闹钟_1_out_16 ));
endmodule
