// Logisim project 1（加法器）.circ as structural Verilog: 5 circuits, main circuit 一位二进制半加器
module \一位二进制半加器  (
  input  A,
  input  B,
  output S,
  output C
);

  wire nand_1_out, nand_2_out, nand_3_out;

  nand nand_1 (nand_1_out, A, B);
  nand nand_2 (nand_2_out, A, nand_1_out);
  nand nand_3 (nand_3_out, nand_1_out, B);
  not not_1 (C, nand_1_out);
  nand nand_4 (S, nand_2_out, nand_3_out);
endmodule

module \一位二进制全加器  (
  input  A,
  input  B,
  input  Ci,
  output S,
  output C0
);

  wire nand_1_out, nand_2_out, xor_1_out;

  xor xor_1 (xor_1_out, A, B);
  nand nand_1 (nand_1_out, B, A);
  xor xor_2 (S, xor_1_out, Ci);
  nand nand_2 (nand_2_out, xor_1_out, Ci);
  nand nand_3 (C0, nand_2_out, nand_1_out);
endmodule

module \串行进位四位二进制加法器  (
  input  A0,
  input  B0,
  input  C0,
  input  A1,
  input  B1,
  input  A2,
  input  B2,
  input  A3,
  input  B3,
  output S0,
  output S1,
  output S2,
  output S3,
  output C4
);

  wire \一位二进制全加器_1_c0 , \一位二进制全加器_2_c0 , \一位二进制全加器_3_c0 ;

  \一位二进制全加器  \u_一位二进制全加器_1  (.A(A0), .B(B0), .Ci(C0), .S(S0), .C0(\一位二进制全加器_1_c0 ));
  \一位二进制全加器  \u_一位二进制全加器_2  (.A(A1), .B(B1), .Ci(\一位二进制全加器_1_c0 ), .S(S1), .C0(\一位二进制全加器_2_c0 ));
  \一位二进制全加器  \u_一位二进制全加器_3  (.A(A2), .B(B2), .Ci(\一位二进制全加器_2_c0 ), .S(S2), .C0(\一位二进制全加器_3_c0 ));
  \一位二进制全加器  \u_一位二进制全加器_4  (.A(A3), .B(B3), .Ci(\一位二进制全加器_3_c0 ), .S(S3), .C0(C4));
endmodule

module \先行进位四位二进制加法器  (
  input  C0,
  input  A0,
  input  A1,
  input  A2,
  input  A3,
  input  B0,
  input  B1,
  input  B2,
  input  B3,
  output S2,
  output S0,
  output S4,
  output S3,
  output C4
);

  wire and_1_out, and_2_out, and_3_out, and_4_out, and_5_out, and_6_out, and_7_out, and_8_out, and_9_out,
       and_10_out, G0_out, G1_out, G2_out, G3_out, or_1_out, or_2_out, or_4_out, P0_out, P1_out, P2_out,
       P3_out, xor_1_out, xor_4_out, xor_6_out, xor_7_out;

  xor xor_1 (xor_1_out, C0, G0_out);
  and G0 (G0_out, A0, B0);
  xor xor_2 (S0, xor_1_out, P0_out);
  and and_1 (and_1_out, C0, P0_out);
  or P0 (P0_out, A0, B0);
  xor xor_3 (S2, xor_4_out, or_1_out);
  xor xor_4 (xor_4_out, G1_out, P1_out);
  or or_1 (or_1_out, and_1_out, G0_out);
  and G1 (G1_out, A1, B1);
  and and_2 (and_2_out, G0_out, P1_out);
  or P1 (P1_out, A1, B1);
  or or_2 (or_2_out, G1_out, and_2_out, and_3_out);
  and and_3 (and_3_out, C0, P0_out, P1_out);
  and G2 (G2_out, A2, B2);
  xor xor_5 (S3, or_2_out, xor_6_out);
  xor xor_6 (xor_6_out, G2_out, P2_out);
  or P2 (P2_out, A2, B2);
  and and_4 (and_4_out, G2_out, P3_out);
  and G3 (G3_out, A3, B3);
  or or_3 (C4, and_4_out, and_5_out, G3_out, and_6_out, and_7_out);
  and and_5 (and_5_out, G1_out, P2_out, P3_out);
  or P3 (P3_out, A3, B3);
  and and_6 (and_6_out, G0_out, P1_out, P2_out, P3_out);
  and and_7 (and_7_out, C0, P0_out, P1_out, P2_out, P3_out);
  xor xor_7 (xor_7_out, G3_out, P3_out);
  buf and_8 (and_8_out, G1_out);  // AND_Gate
  xor xor_8 (S4, xor_7_out, or_4_out);
  or or_4 (or_4_out, and_8_out, G2_out, and_9_out, and_10_out);
  and and_9 (and_9_out, G0_out, P2_out);
  and and_10 (and_10_out, C0, P0_out, P1_out, P2_out);
endmodule

module \先行进位四位二进制加法器测试电路  (
  input  C0,
  input  A3,
  input  A2,
  input  A1,
  input  A0,
  input  B3,
  input  B2,
  input  B1,
  input  B0,
  output S3,
  output S2,
  output S1,
  output S0,
  output C4
);

  \先行进位四位二进制加法器  \u_先行进位四位二进制加法器_1  (
    .S0(S0), .S2(S1), .S3(S2), .C4(C4), .C0(C0), .A0(A0), .A1(A1), .A2(A2), .A3(A3), .B0(B0), .B1(B1),
    .B2(B2), .S4(S3), .B3(B3));
endmodule
