// Logisim project 2（乘法器）.circ as structural Verilog: 6 circuits, main circuit main
module main (
  input  [3:0] a,
  input  [3:0] b,
  output [7:0] out_3
);

  wire [7:0] adder_1_out, adder_2_out, adder_3_out, adder_4_out, bit_extender_1_out, multiplexer_1_out,
       multiplexer_2_out, multiplexer_3_out, shifter_1_out, shifter_2_out, shifter_3_out;

  assign bit_extender_1_out = {{4{1'b0}}, b};  // Bit_Extender bit_extender_1
  Adder adder_1 (.a({8{1'b0}}), .b(bit_extender_1_out), .out(adder_1_out));  // open: cin, cout
  Shifter shifter_1 (.in(bit_extender_1_out), .\dist (3'b001), .out(shifter_1_out));
  Multiplexer #(.width(8)) multiplexer_1 (
    .in0({8{1'b0}}), .in1(adder_1_out), .out(multiplexer_1_out), .sel(a[0]));  // open: en
  Adder adder_2 (.a(multiplexer_1_out), .b(shifter_1_out), .out(adder_2_out));  // open: cin, cout
  Shifter shifter_2 (.in(shifter_1_out), .\dist (3'b001), .out(shifter_2_out));
  Multiplexer #(.width(8)) multiplexer_2 (
    .in0(multiplexer_1_out), .in1(adder_2_out), .out(multiplexer_2_out), .sel(a[1]));  // open: en
  Adder adder_3 (.a(multiplexer_2_out), .b(shifter_2_out), .out(adder_3_out));  // open: cin, cout
  Shifter shifter_3 (.in(shifter_2_out), .\dist (3'b001), .out(shifter_3_out));
  Multiplexer #(.width(8)) multiplexer_3 (
    .in0(multiplexer_2_out), .in1(adder_3_out), .out(multiplexer_3_out), .sel(a[2]));  // open: en
  Adder adder_4 (.a(multiplexer_3_out), .b(shifter_3_out), .out(adder_4_out));  // open: cin, cout
  Multiplexer #(.width(8)) multiplexer_4 (
    .in0(multiplexer_3_out), .in1(adder_4_out), .out(out_3), .sel(a[3]));  // open: en
endmodule

module \_32_4乘法器  (
  input  [3:0] a,
  input  [31:0] in_2,
  output [31:0] out_3
);

  wire [31:0] adder_1_out, adder_2_out, adder_3_out, adder_4_out, multiplexer_1_out, multiplexer_2_out,
       multiplexer_3_out, shifter_1_out, shifter_2_out, shifter_3_out;

  Adder #(.width(32)) adder_1 (.a({32{1'b0}}), .b(in_2), .out(adder_1_out));  // open: cin, cout
  Shifter #(.width(32)) shifter_1 (.in(in_2), .\dist (5'b00001), .out(shifter_1_out));
  Multiplexer #(.width(32)) multiplexer_1 (
    .in0({32{1'b0}}), .in1(adder_1_out), .out(multiplexer_1_out), .sel(a[0]));  // open: en
  Adder #(.width(32)) adder_2 (.a(multiplexer_1_out), .b(shifter_1_out), .out(adder_2_out));  // open: cin, cout
  Shifter #(.width(32)) shifter_2 (.in(shifter_1_out), .\dist (5'b00001), .out(shifter_2_out));
  Multiplexer #(.width(32)) multiplexer_2 (
    .in0(multiplexer_1_out), .in1(adder_2_out), .out(multiplexer_2_out), .sel(a[1]));  // open: en
  Adder #(.width(32)) adder_3 (.a(multiplexer_2_out), .b(shifter_2_out), .out(adder_3_out));  // open: cin, cout
  Shifter #(.width(32)) shifter_3 (.in(shifter_2_out), .\dist (5'b00001), .out(shifter_3_out));
  Multiplexer #(.width(32)) multiplexer_3 (
    .in0(multiplexer_2_out), .in1(adder_3_out), .out(multiplexer_3_out), .sel(a[2]));  // open: en
  Adder #(.width(32)) adder_4 (.a(multiplexer_3_out), .b(shifter_3_out), .out(adder_4_out));  // open: cin, cout
  Multiplexer #(.width(32)) multiplexer_4 (
    .in0(multiplexer_3_out), .in1(adder_4_out), .out(out_3), .sel(a[3]));  // open: en
endmodule

module \_32_32乘法器  (
  input  [31:0] a,
  input  [31:0] b,
  output [31:0] out_3
);

  wire [3:0] bit_extender_1_out, bit_extender_2_out, bit_extender_3_out, bit_extender_4_out,
       bit_extender_5_out, bit_extender_6_out, bit_extender_7_out, bit_extender_8_out;
  wire [31:0] adder_1_out, adder_2_out, adder_3_out, adder_4_out, adder_5_out, adder_6_out,
       \n32_4乘法器_1_out_3 , \n32_4乘法器_2_out_3 , \n32_4乘法器_3_out_3 , \n32_4乘法器_4_out_3 , \n32_4乘法器_5_out_3 ,
       \n32_4乘法器_6_out_3 , \n32_4乘法器_7_out_3 , \n32_4乘法器_8_out_3 , shifter_1_out, shifter_2_out,
       shifter_3_out, shifter_4_out, shifter_5_out, shifter_6_out, shifter_7_out, shifter_8_out,
       shifter_9_out, shifter_10_out, shifter_11_out, shifter_12_out, shifter_13_out, shifter_14_out;

  Shifter #(.width(32), .shift("lr")) shifter_1 (.in(a), .\dist (5'b11100), .out(shifter_1_out));
  Bit_Extender #(.in_width(32), .out_width(4)) bit_extender_1 (.in(shifter_1_out), .out(bit_extender_1_out));
  \_32_4乘法器  \u_32_4乘法器_1  (.a(bit_extender_1_out), .in_2(b), .out_3(\n32_4乘法器_1_out_3 ));
  Shifter #(.width(32), .shift("lr")) shifter_2 (.in(a), .\dist (5'b11000), .out(shifter_2_out));
  Shifter #(.width(32)) shifter_3 (.in(\n32_4乘法器_1_out_3 ), .\dist (5'b11100), .out(shifter_3_out));
  Bit_Extender #(.in_width(32), .out_width(4)) bit_extender_2 (.in(shifter_2_out), .out(bit_extender_2_out));
  \_32_4乘法器  \u_32_4乘法器_2  (.a(bit_extender_2_out), .in_2(b), .out_3(\n32_4乘法器_2_out_3 ));
  Shifter #(.width(32), .shift("lr")) shifter_4 (.in(a), .\dist (5'b10100), .out(shifter_4_out));
  Bit_Extender #(.in_width(32), .out_width(4)) bit_extender_3 (.in(shifter_4_out), .out(bit_extender_3_out));
  Shifter #(.width(32)) shifter_5 (.in(\n32_4乘法器_2_out_3 ), .\dist (5'b11000), .out(shifter_5_out));
  Shifter #(.width(32), .shift("lr")) shifter_6 (.in(a), .\dist (5'b10000), .out(shifter_6_out));
  \_32_4乘法器  \u_32_4乘法器_3  (.a(bit_extender_3_out), .in_2(b), .out_3(\n32_4乘法器_3_out_3 ));
  Shifter #(.width(32)) shifter_7 (.in(\n32_4乘法器_3_out_3 ), .\dist (5'b10100), .out(shifter_7_out));
  Adder #(.width(32)) adder_1 (.a(shifter_5_out), .b(shifter_3_out), .out(adder_1_out));  // open: cin, cout
  Bit_Extender #(.in_width(32), .out_width(4)) bit_extender_4 (.in(shifter_6_out), .out(bit_extender_4_out));
  \_32_4乘法器  \u_32_4乘法器_4  (.a(bit_extender_4_out), .in_2(b), .out_3(\n32_4乘法器_4_out_3 ));
  Adder #(.width(32)) adder_2 (.a(shifter_7_out), .b(adder_1_out), .out(adder_2_out));  // open: cin, cout
  Shifter #(.width(32), .shift("lr")) shifter_8 (.in(a), .\dist (5'b01100), .out(shifter_8_out));
  Bit_Extender #(.in_width(32), .out_width(4)) bit_extender_5 (.in(shifter_8_out), .out(bit_extender_5_out));
  Shifter #(.width(32)) shifter_9 (.in(\n32_4乘法器_4_out_3 ), .\dist (5'b10000), .out(shifter_9_out));
  Shifter #(.width(32), .shift("lr")) shifter_10 (.in(a), .\dist (5'b01000), .out(shifter_10_out));
  \_32_4乘法器  \u_32_4乘法器_5  (.a(bit_extender_5_out), .in_2(b), .out_3(\n32_4乘法器_5_out_3 ));
  Shifter #(.width(32)) shifter_11 (.in(\n32_4乘法器_5_out_3 ), .\dist (5'b01100), .out(shifter_11_out));
  Adder #(.width(32)) adder_3 (.a(shifter_9_out), .b(adder_2_out), .out(adder_3_out));  // open: cin, cout
  Bit_Extender #(.in_width(32), .out_width(4)) bit_extender_6 (.in(shifter_10_out), .out(bit_extender_6_out));
  \_32_4乘法器  \u_32_4乘法器_6  (.a(bit_extender_6_out), .in_2(b), .out_3(\n32_4乘法器_6_out_3 ));
  Adder #(.width(32)) adder_4 (.a(shifter_11_out), .b(adder_3_out), .out(adder_4_out));  // open: cin, cout
  Shifter #(.width(32), .shift("lr")) shifter_12 (.in(a), .\dist (5'b00100), .out(shifter_12_out));
  Bit_Extender #(.in_width(32), .out_width(4)) bit_extender_7 (.in(shifter_12_out), .out(bit_extender_7_out));
  Shifter #(.width(32)) shifter_13 (.in(\n32_4乘法器_6_out_3 ), .\dist (5'b01000), .out(shifter_13_out));
  \_32_4乘法器  \u_32_4乘法器_7  (.a(bit_extender_7_out), .in_2(b), .out_3(\n32_4乘法器_7_out_3 ));
  Shifter #(.width(32)) shifter_14 (.in(\n32_4乘法器_7_out_3 ), .\dist (5'b00100), .out(shifter_14_out));
  Adder #(.width(32)) adder_5 (.a(shifter_13_out), .b(adder_4_out), .out(adder_5_out));  // open: cin, cout
  Bit_Extender #(.in_width(32), .out_width(4)) bit_extender_8 (.in(a), .out(bit_extender_8_out));
  \_32_4乘法器  \u_32_4乘法器_8  (.a(bit_extender_8_out), .in_2(b), .out_3(\n32_4乘法器_8_out_3 ));
  Adder #(.width(32)) adder_6 (.a(shifter_14_out), .b(adder_5_out), .out(adder_6_out));  // open: cin, cout
  Adder #(.width(32)) adder_7 (.a(\n32_4乘法器_8_out_3 ), .b(adder_6_out), .out(out_3));  // open: cin, cout
endmodule

module \_4_4测试  (
  input  [3:0] a,
  input  [3:0] b,
  output [7:0] out_3
);

  main main_1 (.a(a), .b(b), .out_3(out_3));
endmodule

module \_32_4测试  (
  input  [3:0] in_1,
  input  [31:0] in_2,
  output [31:0] out_3
);

  \_32_4乘法器  \u_32_4乘法器_1  (.a(in_1), .in_2(in_2), .out_3(out_3));
endmodule

module \_32_32测试  (
  input  [31:0] a,
  input  [31:0] b,
  output [31:0] out_3
);

  \_32_32乘法器  \u_32_32乘法器_1  (.a(a), .b(b), .out_3(out_3));
endmodule
