// Logisim project 3(除法器).circ as structural Verilog: 4 circuits, main circuit main
module main (
  input  [3:0] n2,
  input  [3:0] d,
  output [3:0] quot,
  output [3:0] rem
);

  wire comparator_1_lt, comparator_2_lt, comparator_3_lt, comparator_4_lt;
  wire [7:0] adder_1_out, adder_2_out, adder_3_out, adder_4_out, adder_5_out, adder_6_out, adder_7_out,
       bit_extender_1_out, bit_extender_2_out, multiplexer_1_out, multiplexer_2_out, multiplexer_3_out,
       multiplexer_4_out, multiplexer_5_out, multiplexer_6_out, multiplexer_7_out, multiplexer_8_out,
       shifter_1_out, shifter_2_out, shifter_3_out, shifter_4_out, shifter_5_out, shifter_6_out,
       shifter_7_out, shifter_8_out, shifter_9_out, shifter_10_out, shifter_11_out, shifter_12_out,
       shifter_13_out, shifter_14_out, shifter_15_out, shifter_16_out, shifter_17_out, shifter_18_out,
       shifter_19_out, subtractor_1_out, subtractor_2_out, subtractor_3_out, subtractor_4_out;

  assign bit_extender_1_out = {{4{1'b0}}, d};  // Bit_Extender bit_extender_1
  assign bit_extender_2_out = {{4{1'b0}}, n2};  // Bit_Extender bit_extender_2
  Shifter shifter_1 (.in(bit_extender_2_out), .\dist (3'b001), .out(shifter_1_out));
  Shifter shifter_2 (.in(shifter_1_out), .\dist (3'b100), .out(shifter_2_out));
  Shifter #(.shift("lr")) shifter_3 (.in(shifter_1_out), .\dist (3'b100), .out(shifter_3_out));
  Comparator #(.mode("unsigned")) comparator_1 (
    .a(shifter_3_out), .b(bit_extender_1_out), .lt(comparator_1_lt));  // open: gt, eq
  Shifter #(.shift("lr")) shifter_4 (.in(shifter_2_out), .\dist (3'b100), .out(shifter_4_out));
  Subtractor subtractor_1 (.a(shifter_3_out), .b(bit_extender_1_out), .out(subtractor_1_out));  // open: bin, bout
  Multiplexer #(.width(8), .enable("false")) multiplexer_1 (
    .in0(subtractor_1_out), .in1(shifter_3_out), .out(multiplexer_1_out), .sel(comparator_1_lt));
  Adder adder_1 (.a(shifter_4_out), .b(8'h1), .out(adder_1_out));  // open: cin, cout
  Shifter shifter_5 (.in(multiplexer_1_out), .\dist (3'b100), .out(shifter_5_out));
  Multiplexer #(.width(8), .enable("false")) multiplexer_2 (
    .in0(adder_1_out), .in1(shifter_4_out), .out(multiplexer_2_out), .sel(comparator_1_lt));
  Adder adder_2 (.a(multiplexer_2_out), .b(shifter_5_out), .out(adder_2_out));  // open: cin, cout
  Shifter shifter_6 (.in(adder_2_out), .\dist (3'b001), .out(shifter_6_out));
  Shifter #(.shift("lr")) shifter_7 (.in(shifter_6_out), .\dist (3'b100), .out(shifter_7_out));
  Shifter shifter_8 (.in(shifter_6_out), .\dist (3'b100), .out(shifter_8_out));
  Comparator #(.mode("unsigned")) comparator_2 (
    .a(shifter_7_out), .b(bit_extender_1_out), .lt(comparator_2_lt));  // open: gt, eq
  Shifter #(.shift("lr")) shifter_9 (.in(shifter_8_out), .\dist (3'b100), .out(shifter_9_out));
  Subtractor subtractor_2 (.a(shifter_7_out), .b(bit_extender_1_out), .out(subtractor_2_out));  // open: bin, bout
  Multiplexer #(.width(8), .enable("false")) multiplexer_3 (
    .in0(subtractor_2_out), .in1(shifter_7_out), .out(multiplexer_3_out), .sel(comparator_2_lt));
  Adder adder_3 (.a(shifter_9_out), .b(8'h1), .out(adder_3_out));  // open: cin, cout
  Multiplexer #(.width(8), .enable("false")) multiplexer_4 (
    .in0(adder_3_out), .in1(shifter_9_out), .out(multiplexer_4_out), .sel(comparator_2_lt));
  Shifter shifter_10 (.in(multiplexer_3_out), .\dist (3'b100), .out(shifter_10_out));
  Adder adder_4 (.a(multiplexer_4_out), .b(shifter_10_out), .out(adder_4_out));  // open: cin, cout
  Shifter shifter_11 (.in(adder_4_out), .\dist (3'b001), .out(shifter_11_out));
  Shifter #(.shift("lr")) shifter_12 (.in(shifter_11_out), .\dist (3'b100), .out(shifter_12_out));
  Shifter shifter_13 (.in(shifter_11_out), .\dist (3'b100), .out(shifter_13_out));
  Comparator #(.mode("unsigned")) comparator_3 (
    .a(shifter_12_out), .b(bit_extender_1_out), .lt(comparator_3_lt));  // open: gt, eq
  Shifter #(.shift("lr")) shifter_14 (.in(shifter_13_out), .\dist (3'b100), .out(shifter_14_out));
  Subtractor subtractor_3 (.a(shifter_12_out), .b(bit_extender_1_out), .out(subtractor_3_out));  // open: bin, bout
  Adder adder_5 (.a(shifter_14_out), .b(8'h1), .out(adder_5_out));  // open: cin, cout
  Multiplexer #(.width(8), .enable("false")) multiplexer_5 (
    .in0(subtractor_3_out), .in1(shifter_12_out), .out(multiplexer_5_out), .sel(comparator_3_lt));
  Multiplexer #(.width(8), .enable("false")) multiplexer_6 (
    .in0(adder_5_out), .in1(shifter_14_out), .out(multiplexer_6_out), .sel(comparator_3_lt));
  Shifter shifter_15 (.in(multiplexer_5_out), .\dist (3'b100), .out(shifter_15_out));
  Adder adder_6 (.a(multiplexer_6_out), .b(shifter_15_out), .out(adder_6_out));  // open: cin, cout
  Shifter shifter_16 (.in(adder_6_out), .\dist (3'b001), .out(shifter_16_out));
  Shifter shifter_17 (.in(shifter_16_out), .\dist (3'b100), .out(shifter_17_out));
  Shifter #(.shift("lr")) shifter_18 (.in(shifter_16_out), .\dist (3'b100), .out(shifter_18_out));
  Comparator #(.mode("unsigned")) comparator_4 (
    .a(shifter_18_out), .b(bit_extender_1_out), .lt(comparator_4_lt));  // open: gt, eq
  Shifter #(.shift("lr")) shifter_19 (.in(shifter_17_out), .\dist (3'b100), .out(shifter_19_out));
  Subtractor subtractor_4 (.a(shifter_18_out), .b(bit_extender_1_out), .out(subtractor_4_out));  // open: bin, bout
  Adder adder_7 (.a(shifter_19_out), .b(8'h1), .out(adder_7_out));  // open: cin, cout
  Multiplexer #(.width(8), .enable("false")) multiplexer_7 (
    .in0(subtractor_4_out), .in1(shifter_18_out), .out(multiplexer_7_out), .sel(comparator_4_lt));
  Multiplexer #(.width(8), .enable("false")) multiplexer_8 (
    .in0(adder_7_out), .in1(shifter_19_out), .out(multiplexer_8_out), .sel(comparator_4_lt));
  Bit_Extender #(.out_width(4)) bit_extender_3 (.in(multiplexer_7_out), .out(rem));
  Bit_Extender #(.out_width(4)) bit_extender_4 (.in(multiplexer_8_out), .out(quot));
endmodule

module div_32 (
  input  [31:0] d,
  input  [31:0] in_2,
  output [31:0] rem,
  output [31:0] quot
);

  wire [31:0] div32_1_1_next_quot, div32_1_1_next_rem, div32_1_2_next_quot, div32_1_2_next_rem,
       div32_1_3_next_quot, div32_1_3_next_rem, div32_1_4_next_quot, div32_1_4_next_rem, div32_1_5_next_quot,
       div32_1_5_next_rem, div32_1_6_next_quot, div32_1_6_next_rem, div32_1_7_next_quot, div32_1_7_next_rem,
       div32_1_8_next_quot, div32_1_8_next_rem, div32_1_9_next_quot, div32_1_9_next_rem,
       div32_1_10_next_quot, div32_1_10_next_rem, div32_1_11_next_quot, div32_1_11_next_rem,
       div32_1_12_next_quot, div32_1_12_next_rem, div32_1_13_next_quot, div32_1_13_next_rem,
       div32_1_14_next_quot, div32_1_14_next_rem, div32_1_15_next_quot, div32_1_15_next_rem,
       div32_1_16_next_quot, div32_1_16_next_rem, div32_1_17_next_quot, div32_1_17_next_rem,
       div32_1_18_next_quot, div32_1_18_next_rem, div32_1_19_next_quot, div32_1_19_next_rem,
       div32_1_20_next_quot, div32_1_20_next_rem, div32_1_21_next_quot, div32_1_21_next_rem,
       div32_1_22_next_quot, div32_1_22_next_rem, div32_1_23_next_quot, div32_1_23_next_rem,
       div32_1_24_next_quot, div32_1_24_next_rem, div32_1_25_next_quot, div32_1_25_next_rem,
       div32_1_26_next_quot, div32_1_26_next_rem, div32_1_27_next_quot, div32_1_27_next_rem,
       div32_1_28_next_quot, div32_1_28_next_rem, div32_1_29_next_quot, div32_1_29_next_rem,
       div32_1_31_next_quot, div32_1_31_next_rem, div32_1_32_next_quot, div32_1_32_next_rem;

  // Probe on div32_1_1_next_rem
  div32_1 div32_1_1 (
    .d(d), .cur_rem({32{1'b0}}), .cur_quot(in_2), .next_rem(div32_1_1_next_rem),
    .next_quot(div32_1_1_next_quot));
  // Probe on div32_1_1_next_quot
  div32_1 div32_1_2 (
    .d(d), .cur_rem(div32_1_1_next_rem), .cur_quot(div32_1_1_next_quot), .next_rem(div32_1_2_next_rem),
    .next_quot(div32_1_2_next_quot));
  div32_1 div32_1_3 (
    .d(d), .cur_rem(div32_1_2_next_rem), .cur_quot(div32_1_2_next_quot), .next_rem(div32_1_3_next_rem),
    .next_quot(div32_1_3_next_quot));
  div32_1 div32_1_4 (
    .d(d), .cur_rem(div32_1_3_next_rem), .cur_quot(div32_1_3_next_quot), .next_rem(div32_1_4_next_rem),
    .next_quot(div32_1_4_next_quot));
  div32_1 div32_1_5 (
    .d(d), .cur_rem(div32_1_4_next_rem), .cur_quot(div32_1_4_next_quot), .next_rem(div32_1_5_next_rem),
    .next_quot(div32_1_5_next_quot));
  div32_1 div32_1_6 (
    .d(d), .cur_rem(div32_1_5_next_rem), .cur_quot(div32_1_5_next_quot), .next_rem(div32_1_6_next_rem),
    .next_quot(div32_1_6_next_quot));
  div32_1 div32_1_7 (
    .d(d), .cur_rem(div32_1_6_next_rem), .cur_quot(div32_1_6_next_quot), .next_rem(div32_1_7_next_rem),
    .next_quot(div32_1_7_next_quot));
  div32_1 div32_1_8 (
    .d(d), .cur_rem(div32_1_7_next_rem), .cur_quot(div32_1_7_next_quot), .next_rem(div32_1_8_next_rem),
    .next_quot(div32_1_8_next_quot));
  div32_1 div32_1_9 (
    .d(d), .cur_rem(div32_1_8_next_rem), .cur_quot(div32_1_8_next_quot), .next_rem(div32_1_9_next_rem),
    .next_quot(div32_1_9_next_quot));
  div32_1 div32_1_10 (
    .d(d), .cur_rem(div32_1_9_next_rem), .cur_quot(div32_1_9_next_quot), .next_rem(div32_1_10_next_rem),
    .next_quot(div32_1_10_next_quot));
  div32_1 div32_1_11 (
    .d(d), .cur_rem(div32_1_10_next_rem), .cur_quot(div32_1_10_next_quot), .next_rem(div32_1_11_next_rem),
    .next_quot(div32_1_11_next_quot));
  div32_1 div32_1_12 (
    .d(d), .cur_rem(div32_1_11_next_rem), .cur_quot(div32_1_11_next_quot), .next_rem(div32_1_12_next_rem),
    .next_quot(div32_1_12_next_quot));
  div32_1 div32_1_13 (
    .d(d), .cur_rem(div32_1_12_next_rem), .cur_quot(div32_1_12_next_quot), .next_rem(div32_1_13_next_rem),
    .next_quot(div32_1_13_next_quot));
  div32_1 div32_1_14 (
    .d(d), .cur_rem(div32_1_13_next_rem), .cur_quot(div32_1_13_next_quot), .next_rem(div32_1_14_next_rem),
    .next_quot(div32_1_14_next_quot));
  div32_1 div32_1_15 (
    .d(d), .cur_rem(div32_1_32_next_rem), .cur_quot(div32_1_32_next_quot), .next_rem(div32_1_15_next_rem),
    .next_quot(div32_1_15_next_quot));
  div32_1 div32_1_16 (
    .d(d), .cur_rem(div32_1_14_next_rem), .cur_quot(div32_1_14_next_quot), .next_rem(div32_1_16_next_rem),
    .next_quot(div32_1_16_next_quot));
  div32_1 div32_1_17 (
    .d(d), .cur_rem(div32_1_15_next_rem), .cur_quot(div32_1_15_next_quot), .next_rem(div32_1_17_next_rem),
    .next_quot(div32_1_17_next_quot));
  div32_1 div32_1_18 (
    .d(d), .cur_rem(div32_1_16_next_rem), .cur_quot(div32_1_16_next_quot), .next_rem(div32_1_18_next_rem),
    .next_quot(div32_1_18_next_quot));
  div32_1 div32_1_19 (
    .d(d), .cur_rem(div32_1_17_next_rem), .cur_quot(div32_1_17_next_quot), .next_rem(div32_1_19_next_rem),
    .next_quot(div32_1_19_next_quot));
  div32_1 div32_1_20 (
    .d(d), .cur_rem(div32_1_18_next_rem), .cur_quot(div32_1_18_next_quot), .next_rem(div32_1_20_next_rem),
    .next_quot(div32_1_20_next_quot));
  div32_1 div32_1_21 (
    .d(d), .cur_rem(div32_1_19_next_rem), .cur_quot(div32_1_19_next_quot), .next_rem(div32_1_21_next_rem),
    .next_quot(div32_1_21_next_quot));
  div32_1 div32_1_22 (
    .d(d), .cur_rem(div32_1_20_next_rem), .cur_quot(div32_1_20_next_quot), .next_rem(div32_1_22_next_rem),
    .next_quot(div32_1_22_next_quot));
  div32_1 div32_1_23 (
    .d(d), .cur_rem(div32_1_22_next_rem), .cur_quot(div32_1_22_next_quot), .next_rem(div32_1_23_next_rem),
    .next_quot(div32_1_23_next_quot));
  div32_1 div32_1_24 (
    .d(d), .cur_rem(div32_1_21_next_rem), .cur_quot(div32_1_21_next_quot), .next_rem(div32_1_24_next_rem),
    .next_quot(div32_1_24_next_quot));
  div32_1 div32_1_25 (
    .d(d), .cur_rem(div32_1_23_next_rem), .cur_quot(div32_1_23_next_quot), .next_rem(div32_1_25_next_rem),
    .next_quot(div32_1_25_next_quot));
  div32_1 div32_1_26 (
    .d(d), .cur_rem(div32_1_24_next_rem), .cur_quot(div32_1_24_next_quot), .next_rem(div32_1_26_next_rem),
    .next_quot(div32_1_26_next_quot));
  div32_1 div32_1_27 (
    .d(d), .cur_rem(div32_1_25_next_rem), .cur_quot(div32_1_25_next_quot), .next_rem(div32_1_27_next_rem),
    .next_quot(div32_1_27_next_quot));
  div32_1 div32_1_28 (
    .d(d), .cur_rem(div32_1_26_next_rem), .cur_quot(div32_1_26_next_quot), .next_rem(div32_1_28_next_rem),
    .next_quot(div32_1_28_next_quot));
  div32_1 div32_1_29 (
    .d(d), .cur_rem(div32_1_27_next_rem), .cur_quot(div32_1_27_next_quot), .next_rem(div32_1_29_next_rem),
    .next_quot(div32_1_29_next_quot));
  div32_1 div32_1_30 (
    .d(d), .cur_rem(div32_1_28_next_rem), .cur_quot(div32_1_28_next_quot), .next_rem(rem), .next_quot(quot));
  div32_1 div32_1_31 (
    .d(d), .cur_rem(div32_1_29_next_rem), .cur_quot(div32_1_29_next_quot), .next_rem(div32_1_31_next_rem),
    .next_quot(div32_1_31_next_quot));
  div32_1 div32_1_32 (
    .d(d), .cur_rem(div32_1_31_next_rem), .cur_quot(div32_1_31_next_quot), .next_rem(div32_1_32_next_rem),
    .next_quot(div32_1_32_next_quot));
endmodule

module div32_1 (
  input  [31:0] d,
  input  [31:0] cur_rem,
  input  [31:0] cur_quot,
  output [31:0] next_rem,
  output [31:0] next_quot
);

  wire comparator_1_gt;
  wire [31:0] or_1_out, or_2_out, shifter_1_out, shifter_2_out, shifter_3_out, subtractor_1_out;

  Shifter #(.width(32)) shifter_1 (.in(cur_rem), .\dist (5'b00001), .out(shifter_1_out));
  Shifter #(.width(32), .shift("lr")) shifter_2 (.in(cur_quot), .\dist ({5{1'b1}}), .out(shifter_2_out));
  Shifter #(.width(32)) shifter_3 (.in(cur_quot), .\dist (5'b00001), .out(shifter_3_out));
  assign or_1_out = shifter_1_out | shifter_2_out;  // OR_Gate or_1, 32 bits wide
  Comparator #(.width(32)) comparator_1 (.a(d), .b(or_1_out), .gt(comparator_1_gt));  // open: eq, lt
  assign or_2_out = 32'h1 | shifter_3_out;  // OR_Gate or_2, 32 bits wide
  Subtractor #(.width(32)) subtractor_1 (.a(or_1_out), .b(d), .out(subtractor_1_out));  // open: bin, bout
  Multiplexer #(.width(32), .enable("false")) multiplexer_1 (
    .in0(or_2_out), .in1(shifter_3_out), .out(next_quot), .sel(comparator_1_gt));
  Multiplexer #(.width(32), .enable("false")) multiplexer_2 (
    .in0(subtractor_1_out), .in1(or_1_out), .out(next_rem), .sel(comparator_1_gt));
endmodule

module test (
  input  [31:0] n,
  input  [31:0] d,
  input  [3:0] n2,
  input  [3:0] d_2,
  output [31:0] quot,
  output [31:0] rem,
  output [3:0] quot_2,
  output [3:0] rem_2
);

  div_32 div_32_1 (.d(d), .rem(rem), .quot(quot), .in_2(n));
  main main_1 (.n2(n2), .d(d_2), .quot(quot_2), .rem(rem_2));
endmodule
