// Logisim project 4 小型门禁.circ as structural Verilog: 9 circuits, main circuit test
module main (
  input  cpr,
  input  D,
  input  C,
  input  B,
  input  A,
  input  LC,
  input  cpu,
  input  cpd,
  output QD,
  output QC,
  output QB,
  output QA
);

  wire and_1_out, and_2_out, and_3_out, and_4_out, and_5_out, and_6_out, and_7_out, and_8_out, and_9_out,
       and_10_out, and_11_out, and_12_out, and_13_out, and_14_out, d_ff_1_qn, d_ff_2_qn, d_ff_3_qn,
       d_ff_4_qn, not_1_out, not_2_out, not_3_out, not_4_out, not_5_out, or_1_out, or_2_out, or_3_out,
       or_4_out, or_5_out, or_6_out, or_7_out, or_8_out;

  not not_1 (not_1_out, LC);
  or or_1 (or_1_out, and_2_out, and_1_out);
  and and_1 (and_1_out, cpu, QB, QA, QC);
  and and_2 (and_2_out, cpd, d_ff_3_qn, d_ff_4_qn, d_ff_2_qn);
  D_Flip_Flop #(.trigger("falling"), .Pre_Clr_Positions("LEGACY"), .NegatePresetClear("false"), .enable("false"), .NewFFLayout("false")) d_ff_1 (
    .clk(or_1_out), .D(d_ff_1_qn), .Q(QD), .Qn(d_ff_1_qn), .preset(and_3_out), .reset(or_2_out));
  or or_2 (or_2_out, and_4_out, cpr);
  not not_2 (not_2_out, D);
  and and_3 (and_3_out, D, not_1_out);
  and and_4 (and_4_out, not_1_out, not_2_out);
  or or_3 (or_3_out, and_5_out, and_6_out);
  and and_5 (and_5_out, cpd, d_ff_4_qn, d_ff_3_qn);
  and and_6 (and_6_out, cpu, QA, QB);
  D_Flip_Flop #(.trigger("falling"), .Pre_Clr_Positions("LEGACY"), .NegatePresetClear("false"), .enable("false"), .NewFFLayout("false")) d_ff_2 (
    .clk(or_3_out), .D(d_ff_2_qn), .Q(QC), .Qn(d_ff_2_qn), .preset(and_7_out), .reset(or_4_out));
  or or_4 (or_4_out, cpr, and_8_out);
  and and_7 (and_7_out, C, not_1_out);
  and and_8 (and_8_out, not_1_out, not_3_out);
  not not_3 (not_3_out, C);
  or or_5 (or_5_out, and_9_out, and_10_out);
  and and_9 (and_9_out, cpd, d_ff_4_qn);
  and and_10 (and_10_out, cpu, QA);
  D_Flip_Flop #(.trigger("falling"), .Pre_Clr_Positions("LEGACY"), .NegatePresetClear("false"), .enable("false"), .NewFFLayout("false")) d_ff_3 (
    .clk(or_5_out), .D(d_ff_3_qn), .Q(QB), .Qn(d_ff_3_qn), .preset(and_11_out), .reset(or_6_out));
  or or_6 (or_6_out, and_12_out, cpr);
  and and_11 (and_11_out, B, not_1_out);
  and and_12 (and_12_out, not_1_out, not_4_out);
  not not_4 (not_4_out, B);
  or or_7 (or_7_out, cpd, cpu);
  D_Flip_Flop #(.trigger("falling"), .Pre_Clr_Positions("LEGACY"), .NegatePresetClear("false"), .enable("false"), .NewFFLayout("false")) d_ff_4 (
    .clk(or_7_out), .D(d_ff_4_qn), .Q(QA), .Qn(d_ff_4_qn), .preset(and_13_out), .reset(or_8_out));
  or or_8 (or_8_out, and_14_out, cpr);
  and and_13 (and_13_out, A, not_1_out);
  and and_14 (and_14_out, not_1_out, not_5_out);
  not not_5 (not_5_out, A);
endmodule

module test (
  input  in_1,
  input  in_2,
  input  in_3,
  input  in_4,
  input  in_5,
  input  in_6,
  input  in_7,
  input  in_8,
  output out_9,
  output out_10,
  output out_11,
  output out_12
);

  main main_1 (
    .D(in_4), .cpr(in_2), .cpu(in_1), .cpd(in_3), .LC(in_8), .QD(out_9), .QC(out_10), .QB(out_11),
    .QA(out_12), .C(in_5), .B(in_6), .A(in_7));
endmodule

module \二进制转8421_BCD码  (
  input  A3,
  input  A2,
  input  A1,
  input  A0,
  output S80,
  output S40,
  output S20,
  output S10,
  output S8,
  output S4,
  output S2,
  output S1
);

  wire and_1_out, or_1_out;

  or or_1 (or_1_out, A1, A2);
  \先行进位4位二进制加法  \u_先行进位4位二进制加法_1  (
    .S0(S1), .S1(S2), .S2(S4), .C4(S10), .C0(1'b0), .A0(A0), .A1(A1), .A2(A2), .A3(A3), .B0(1'b0),
    .B1(and_1_out), .B2(and_1_out), .S3(S8), .B3(1'b0));
  and and_1 (and_1_out, A3, or_1_out);

  assign S20 = 1'b0;
  assign S40 = 1'b0;
  assign S80 = 1'b0;
endmodule

module \先行进位4位二进制加法  (
  input  C0,
  input  A0,
  input  A1,
  input  A2,
  input  A3,
  input  B0,
  input  B1,
  input  B2,
  input  B3,
  output S1,
  output S0,
  output S3,
  output S2,
  output C4
);

  wire and_1_out, and_2_out, and_3_out, and_4_out, and_5_out, and_6_out, and_7_out, and_8_out, and_9_out,
       and_10_out, G0_out, G1_out, G2_out, G3_out, or_1_out, or_2_out, or_4_out, P0_out, P1_out, P2_out,
       P3_out, xor_1_out, xor_4_out, xor_6_out, xor_7_out;

  xor xor_1 (xor_1_out, C0, G0_out);
  and G0 (G0_out, A0, B0);
  xor xor_2 (S0, xor_1_out, P0_out);
  and and_1 (and_1_out, C0, P0_out);
  or P0 (P0_out, A0, B0);
  xor xor_3 (S1, xor_4_out, or_1_out);
  xor xor_4 (xor_4_out, G1_out, P1_out);
  or or_1 (or_1_out, and_1_out, G0_out);
  and G1 (G1_out, A1, B1);
  and and_2 (and_2_out, G0_out, P1_out);
  or P1 (P1_out, A1, B1);
  or or_2 (or_2_out, G1_out, and_2_out, and_3_out);
  and and_3 (and_3_out, C0, P0_out, P1_out);
  and G2 (G2_out, A2, B2);
  xor xor_5 (S2, or_2_out, xor_6_out);
  xor xor_6 (xor_6_out, G2_out, P2_out);
  or P2 (P2_out, A2, B2);
  and and_4 (and_4_out, G2_out, P3_out);
  and G3 (G3_out, A3, B3);
  or or_3 (C4, and_4_out, and_5_out, G3_out, and_6_out, and_7_out);
  and and_5 (and_5_out, G1_out, P2_out, P3_out);
  or P3 (P3_out, A3, B3);
  and and_6 (and_6_out, G0_out, P1_out, P2_out, P3_out);
  and and_7 (and_7_out, C0, P0_out, P1_out, P2_out, P3_out);
  xor xor_7 (xor_7_out, G3_out, P3_out);
  buf and_8 (and_8_out, G1_out);  // AND_Gate
  xor xor_8 (S3, xor_7_out, or_4_out);
  or or_4 (or_4_out, and_8_out, G2_out, and_9_out, and_10_out);
  and and_9 (and_9_out, G0_out, P2_out);
  and and_10 (and_10_out, C0, P0_out, P1_out, P2_out);
endmodule

module \_7段译码器  (
  input  A3,
  input  A2,
  input  A1,
  input  A0,
  output a,
  output b,
  output c,
  output d,
  output e,
  output f,
  output g
);

  wire and_1_out, and_2_out, and_3_out, and_4_out, and_5_out, and_6_out, and_7_out, and_8_out, and_9_out,
       and_10_out, and_11_out, and_12_out, and_13_out, and_14_out, and_15_out, and_16_out, and_17_out,
       and_18_out, and_19_out, and_20_out, and_21_out, not_1_out, not_2_out, not_3_out, not_4_out;

  not not_1 (not_1_out, A3);
  not not_2 (not_2_out, A2);
  not not_3 (not_3_out, A1);
  not not_4 (not_4_out, A0);
  and and_1 (and_1_out, not_2_out, not_3_out, not_4_out);
  and and_2 (and_2_out, not_1_out, not_2_out, A1);
  and and_3 (and_3_out, not_1_out, A2, A0);
  and and_4 (and_4_out, A3, not_3_out, A0);
  and and_5 (and_5_out, not_1_out, A1, A0);
  and and_6 (and_6_out, not_1_out, not_2_out);
  and and_7 (and_7_out, not_3_out, not_4_out);
  and and_8 (and_8_out, not_2_out, not_3_out);
  and and_9 (and_9_out, not_1_out, A2);
  and and_10 (and_10_out, not_2_out, A0);
  and and_11 (and_11_out, not_2_out, not_4_out);
  and and_12 (and_12_out, A2, not_3_out, A0);
  and and_13 (and_13_out, not_2_out, A1, A0);
  and and_14 (and_14_out, A2, not_4_out, A1);
  and and_15 (and_15_out, A1, not_4_out);
  and and_16 (and_16_out, not_3_out, not_4_out);
  and and_17 (and_17_out, A2, not_3_out);
  and and_18 (and_18_out, A2, not_4_out);
  and and_19 (and_19_out, A3, not_2_out, not_3_out);
  and and_20 (and_20_out, A3, not_2_out);
  and and_21 (and_21_out, not_2_out, A1);
  or or_1 (a, and_1_out, and_2_out, and_3_out, and_4_out);
  or or_2 (b, and_5_out, and_6_out, and_7_out, and_8_out);
  or or_3 (c, and_8_out, and_9_out, and_10_out);
  or or_4 (d, and_11_out, and_12_out, and_13_out, and_14_out);
  or or_5 (e, and_11_out, and_15_out);
  or or_6 (f, and_16_out, and_17_out, and_18_out, and_19_out);
  or or_7 (g, and_15_out, and_17_out, and_20_out, and_21_out);
endmodule

module \_7段数码显示管  (
  input  in_1,
  input  in_2,
  input  in_3,
  input  in_4
);

  wire \n7段译码器_1_a , \n7段译码器_1_b , \n7段译码器_1_c , \n7段译码器_1_d , \n7段译码器_1_e , \n7段译码器_1_f , \n7段译码器_1_g ,
       \n7段译码器_2_a , \n7段译码器_2_b , \n7段译码器_2_c , \n7段译码器_2_d , \n7段译码器_2_e , \n7段译码器_2_f , \n7段译码器_2_g ,
       \二进制转8421_bcd码_1_s1 , \二进制转8421_bcd码_1_s2 , \二进制转8421_bcd码_1_s4 , \二进制转8421_bcd码_1_s8 ,
       \二进制转8421_bcd码_1_s10 , \二进制转8421_bcd码_1_s20 , \二进制转8421_bcd码_1_s40 , \二进制转8421_bcd码_1_s80 ;

  _7_Segment_Display #(.active("true")) u_7_segment_display_1 (
    .g(\n7段译码器_1_g ), .f(\n7段译码器_1_f ), .a(\n7段译码器_1_a ), .b(\n7段译码器_1_b ), .e(\n7段译码器_1_e ),
    .d(\n7段译码器_1_d ), .c(\n7段译码器_1_c ));  // open: dp
  \_7段译码器  \u_7段译码器_1  (
    .A3(\二进制转8421_bcd码_1_s80 ), .A2(\二进制转8421_bcd码_1_s40 ), .A1(\二进制转8421_bcd码_1_s20 ),
    .A0(\二进制转8421_bcd码_1_s10 ), .a(\n7段译码器_1_a ), .b(\n7段译码器_1_b ), .c(\n7段译码器_1_c ), .d(\n7段译码器_1_d ),
    .e(\n7段译码器_1_e ), .f(\n7段译码器_1_f ), .g(\n7段译码器_1_g ));
  \二进制转8421_BCD码  \u_二进制转8421_bcd码_1  (
    .S80(\二进制转8421_bcd码_1_s80 ), .S40(\二进制转8421_bcd码_1_s40 ), .S20(\二进制转8421_bcd码_1_s20 ),
    .S10(\二进制转8421_bcd码_1_s10 ), .S8(\二进制转8421_bcd码_1_s8 ), .S4(\二进制转8421_bcd码_1_s4 ),
    .S2(\二进制转8421_bcd码_1_s2 ), .S1(\二进制转8421_bcd码_1_s1 ), .A3(in_1), .A2(in_2), .A1(in_3), .A0(in_4));
  _7_Segment_Display #(.active("true")) u_7_segment_display_2 (
    .g(\n7段译码器_2_g ), .f(\n7段译码器_2_f ), .a(\n7段译码器_2_a ), .b(\n7段译码器_2_b ), .e(\n7段译码器_2_e ),
    .d(\n7段译码器_2_d ), .c(\n7段译码器_2_c ));  // open: dp
  \_7段译码器  \u_7段译码器_2  (
    .A3(\二进制转8421_bcd码_1_s8 ), .A2(\二进制转8421_bcd码_1_s4 ), .A1(\二进制转8421_bcd码_1_s2 ),
    .A0(\二进制转8421_bcd码_1_s1 ), .a(\n7段译码器_2_a ), .b(\n7段译码器_2_b ), .c(\n7段译码器_2_c ), .d(\n7段译码器_2_d ),
    .e(\n7段译码器_2_e ), .f(\n7段译码器_2_f ), .g(\n7段译码器_2_g ));
endmodule

module \报警电路  (
  input  cpu,
  input  CLR,
  input  cpd,
  output out_4,
  output out_5,
  output out_6,
  output out_7
);

  wire and_1_out, and_2_out, and_3_out, and_4_out, not_1_out, not_2_out, or_1_out;

  LED #(.active("true")) led_1 (.in(and_1_out));
  and and_1 (and_1_out, cpu, and_2_out);
  not not_1 (not_1_out, and_2_out);
  or or_1 (or_1_out, out_7, out_6, out_5, out_4);
  and and_2 (and_2_out, out_7, out_6, out_5, out_4);
  and and_3 (and_3_out, not_1_out, cpu);
  and and_4 (and_4_out, or_1_out, cpd);
  main main_1 (
    .D(1'b0), .cpr(CLR), .cpu(and_3_out), .cpd(and_4_out), .LC(not_2_out), .QD(out_4), .QC(out_5),
    .QB(out_6), .QA(out_7), .C(1'b0), .B(1'b0), .A(1'b0));
  not not_2 (not_2_out, 1'b0);
endmodule

module \门禁系统电路  (
  input  cpu,
  input  CLR,
  input  cpd,
  output out_4,
  output out_5,
  output out_6,
  output out_7,
  output out_8,
  output out_9,
  output out_10,
  output out_11,
  output out_12,
  output out_13,
  output out_14,
  output out_15,
  output out_16,
  output out_17,
  output out_18
);

  wire and_2_out, and_3_out, and_4_out, main_1_qa, main_1_qb, main_1_qc, main_1_qd, not_1_out, not_2_out,
       or_1_out, \二进制转8421_bcd码_1_s1 , \二进制转8421_bcd码_1_s2 , \二进制转8421_bcd码_1_s4 , \二进制转8421_bcd码_1_s8 ,
       \二进制转8421_bcd码_1_s10 , \二进制转8421_bcd码_1_s20 , \二进制转8421_bcd码_1_s40 , \二进制转8421_bcd码_1_s80 ;

  and and_1 (out_18, cpu, and_4_out);
  not not_1 (not_1_out, and_4_out);
  and and_2 (and_2_out, not_1_out, cpu);
  and and_3 (and_3_out, or_1_out, cpd);
  \二进制转8421_BCD码  \u_二进制转8421_bcd码_1  (
    .S80(\二进制转8421_bcd码_1_s80 ), .S40(\二进制转8421_bcd码_1_s40 ), .S20(\二进制转8421_bcd码_1_s20 ),
    .S10(\二进制转8421_bcd码_1_s10 ), .S8(\二进制转8421_bcd码_1_s8 ), .S4(\二进制转8421_bcd码_1_s4 ),
    .S2(\二进制转8421_bcd码_1_s2 ), .S1(\二进制转8421_bcd码_1_s1 ), .A3(main_1_qd), .A2(main_1_qc), .A1(main_1_qb),
    .A0(main_1_qa));
  or or_1 (or_1_out, main_1_qa, main_1_qb, main_1_qc, main_1_qd);
  and and_4 (and_4_out, main_1_qa, main_1_qb, main_1_qc, main_1_qd);
  \_7段译码器  \u_7段译码器_1  (
    .A3(\二进制转8421_bcd码_1_s80 ), .A2(\二进制转8421_bcd码_1_s40 ), .A1(\二进制转8421_bcd码_1_s20 ),
    .A0(\二进制转8421_bcd码_1_s10 ), .a(out_4), .b(out_5), .c(out_6), .d(out_7), .e(out_8), .f(out_9), .g(out_10));
  main main_1 (
    .D(1'b0), .cpr(CLR), .cpu(and_2_out), .cpd(and_3_out), .LC(not_2_out), .QD(main_1_qd), .QC(main_1_qc),
    .QB(main_1_qb), .QA(main_1_qa), .C(1'b0), .B(1'b0), .A(1'b0));
  not not_2 (not_2_out, 1'b0);
  \_7段译码器  \u_7段译码器_2  (
    .A3(\二进制转8421_bcd码_1_s8 ), .A2(\二进制转8421_bcd码_1_s4 ), .A1(\二进制转8421_bcd码_1_s2 ),
    .A0(\二进制转8421_bcd码_1_s1 ), .a(out_11), .b(out_12), .c(out_13), .d(out_14), .e(out_15), .f(out_16),
    .g(out_17));
endmodule

module \门禁系统封装  (
  input  cpu,
  input  CLR,
  input  CPD
);

  wire \门禁系统电路_1_out_4 , \门禁系统电路_1_out_5 , \门禁系统电路_1_out_6 , \门禁系统电路_1_out_7 , \门禁系统电路_1_out_8 ,
       \门禁系统电路_1_out_9 , \门禁系统电路_1_out_10 , \门禁系统电路_1_out_11 , \门禁系统电路_1_out_12 , \门禁系统电路_1_out_13 ,
       \门禁系统电路_1_out_14 , \门禁系统电路_1_out_15 , \门禁系统电路_1_out_16 , \门禁系统电路_1_out_17 , \门禁系统电路_1_out_18 ;

  _7_Segment_Display #(.active("true")) u_7_segment_display_1 (
    .g(\门禁系统电路_1_out_10 ), .f(\门禁系统电路_1_out_9 ), .a(\门禁系统电路_1_out_4 ), .b(\门禁系统电路_1_out_5 ),
    .e(\门禁系统电路_1_out_8 ), .d(\门禁系统电路_1_out_7 ), .c(\门禁系统电路_1_out_6 ));  // open: dp
  _7_Segment_Display #(.active("true")) u_7_segment_display_2 (
    .g(\门禁系统电路_1_out_17 ), .f(\门禁系统电路_1_out_16 ), .a(\门禁系统电路_1_out_11 ), .b(\门禁系统电路_1_out_12 ),
    .e(\门禁系统电路_1_out_15 ), .d(\门禁系统电路_1_out_14 ), .c(\门禁系统电路_1_out_13 ));  // open: dp
  LED #(.active("true")) led_1 (.in(\门禁系统电路_1_out_18 ));
  \门禁系统电路  \u_门禁系统电路_1  (
    .cpu(cpu), .CLR(CLR), .cpd(CPD), .out_18(\门禁系统电路_1_out_18 ), .out_4(\门禁系统电路_1_out_4 ),
    .out_5(\门禁系统电路_1_out_5 ), .out_6(\门禁系统电路_1_out_6 ), .out_7(\门禁系统电路_1_out_7 ), .out_8(\门禁系统电路_1_out_8 ),
    .out_9(\门禁系统电路_1_out_9 ), .out_10(\门禁系统电路_1_out_10 ), .out_11(\门禁系统电路_1_out_11 ),
    .out_12(\门禁系统电路_1_out_12 ), .out_13(\门禁系统电路_1_out_13 ), .out_14(\门禁系统电路_1_out_14 ),
    .out_15(\门禁系统电路_1_out_15 ), .out_16(\门禁系统电路_1_out_16 ), .out_17(\门禁系统电路_1_out_17 ));
endmodule
