// Logisim project 5 电子钟.circ as structural Verilog: 13 circuits, main circuit 先行进位4位二进制加法器
module \先行进位4位二进制加法器  (
  input  C0,
  input  A0,
  input  A1,
  input  A2,
  input  A3,
  input  B0,
  input  B1,
  input  B2,
  input  B3,
  output S1,
  output S0,
  output S3,
  output S2,
  output C4
);

  wire and_1_out, and_2_out, and_3_out, and_4_out, and_5_out, and_6_out, and_7_out, and_8_out, and_9_out,
       and_10_out, G0_out, G1_out, G2_out, G3_out, or_1_out, or_2_out, or_4_out, P0_out, P1_out, P2_out,
       P3_out, xor_1_out, xor_4_out, xor_6_out, xor_7_out;

  xor xor_1 (xor_1_out, C0, G0_out);
  and G0 (G0_out, A0, B0);
  xor xor_2 (S0, xor_1_out, P0_out);
  and and_1 (and_1_out, C0, P0_out);
  or P0 (P0_out, A0, B0);
  xor xor_3 (S1, xor_4_out, or_1_out);
  xor xor_4 (xor_4_out, G1_out, P1_out);
  or or_1 (or_1_out, and_1_out, G0_out);
  and G1 (G1_out, A1, B1);
  and and_2 (and_2_out, G0_out, P1_out);
  or P1 (P1_out, A1, B1);
  or or_2 (or_2_out, G1_out, and_2_out, and_3_out);
  and and_3 (and_3_out, C0, P0_out, P1_out);
  and G2 (G2_out, A2, B2);
  xor xor_5 (S2, or_2_out, xor_6_out);
  xor xor_6 (xor_6_out, G2_out, P2_out);
  or P2 (P2_out, A2, B2);
  and and_4 (and_4_out, G2_out, P3_out);
  and G3 (G3_out, A3, B3);
  or or_3 (C4, and_4_out, and_5_out, G3_out, and_6_out, and_7_out);
  and and_5 (and_5_out, G1_out, P2_out, P3_out);
  or P3 (P3_out, A3, B3);
  and and_6 (and_6_out, G0_out, P1_out, P2_out, P3_out);
  and and_7 (and_7_out, C0, P0_out, P1_out, P2_out, P3_out);
  xor xor_7 (xor_7_out, G3_out, P3_out);
  buf and_8 (and_8_out, G1_out);  // AND_Gate
  xor xor_8 (S3, xor_7_out, or_4_out);
  or or_4 (or_4_out, and_8_out, G2_out, and_9_out, and_10_out);
  and and_9 (and_9_out, G0_out, P2_out);
  and and_10 (and_10_out, C0, P0_out, P1_out, P2_out);
endmodule

module \四位二进制可逆计数器  (
  input  clr,
  input  D,
  input  C,
  input  B,
  input  A,
  input  nLC,
  input  cpu,
  input  cpd,
  output QD,
  output QC,
  output QB,
  output QA
);

  wire and_1_out, and_2_out, and_3_out, and_4_out, and_5_out, and_6_out, and_7_out, and_8_out, and_9_out,
       and_10_out, and_11_out, and_12_out, and_13_out, and_14_out, d_ff_1_qn, d_ff_2_qn, d_ff_3_qn,
       d_ff_4_qn, not_1_out, not_2_out, not_3_out, not_4_out, not_5_out, or_1_out, or_2_out, or_3_out,
       or_4_out, or_5_out, or_6_out, or_7_out, or_8_out;

  not not_1 (not_1_out, nLC);
  or or_1 (or_1_out, and_2_out, and_1_out);
  and and_1 (and_1_out, cpu, QB, QA, QC);
  and and_2 (and_2_out, cpd, d_ff_3_qn, d_ff_4_qn, d_ff_2_qn);
  D_Flip_Flop #(.trigger("falling"), .Pre_Clr_Positions("LEGACY"), .NegatePresetClear("false"), .enable("false"), .NewFFLayout("false")) d_ff_1 (
    .clk(or_1_out), .D(d_ff_1_qn), .Q(QD), .Qn(d_ff_1_qn), .preset(and_3_out), .reset(or_2_out));
  or or_2 (or_2_out, and_4_out, clr);
  not not_2 (not_2_out, D);
  and and_3 (and_3_out, D, not_1_out);
  and and_4 (and_4_out, not_1_out, not_2_out);
  or or_3 (or_3_out, and_5_out, and_6_out);
  and and_5 (and_5_out, cpd, d_ff_4_qn, d_ff_3_qn);
  and and_6 (and_6_out, cpu, QA, QB);
  D_Flip_Flop #(.trigger("falling"), .Pre_Clr_Positions("LEGACY"), .NegatePresetClear("false"), .enable("false"), .NewFFLayout("false")) d_ff_2 (
    .clk(or_3_out), .D(d_ff_2_qn), .Q(QC), .Qn(d_ff_2_qn), .preset(and_7_out), .reset(or_4_out));
  or or_4 (or_4_out, clr, and_8_out);
  and and_7 (and_7_out, C, not_1_out);
  and and_8 (and_8_out, not_1_out, not_3_out);
  not not_3 (not_3_out, C);
  or or_5 (or_5_out, and_10_out, and_9_out);
  and and_9 (and_9_out, cpu, QA);
  and and_10 (and_10_out, cpd, d_ff_4_qn);
  D_Flip_Flop #(.trigger("falling"), .Pre_Clr_Positions("LEGACY"), .NegatePresetClear("false"), .enable("false"), .NewFFLayout("false")) d_ff_3 (
    .clk(or_5_out), .D(d_ff_3_qn), .Q(QB), .Qn(d_ff_3_qn), .preset(and_11_out), .reset(or_6_out));
  or or_6 (or_6_out, and_12_out, clr);
  and and_11 (and_11_out, B, not_1_out);
  and and_12 (and_12_out, not_1_out, not_4_out);
  not not_4 (not_4_out, B);
  or or_7 (or_7_out, cpd, cpu);
  D_Flip_Flop #(.trigger("falling"), .Pre_Clr_Positions("LEGACY"), .NegatePresetClear("false"), .enable("false"), .NewFFLayout("false")) d_ff_4 (
    .clk(or_7_out), .D(d_ff_4_qn), .Q(QA), .Qn(d_ff_4_qn), .preset(and_13_out), .reset(or_8_out));
  or or_8 (or_8_out, and_14_out, clr);
  and and_13 (and_13_out, A, not_1_out);
  and and_14 (and_14_out, not_1_out, not_5_out);
  not not_5 (not_5_out, A);
endmodule

module \六十进制计数器  (
  input  adj,
  input  CPU,
  input  CLR,
  input  CPD,
  output Q1D,
  output Q1C,
  output Q1B,
  output Q1A,
  output Q0D,
  output Q0C,
  output Q0B,
  output Q0A,
  output nQCC
);

  wire and_1_out, and_2_out, and_3_out, and_4_out, comparator_1_eq, comparator_2_eq, nor_1_out, not_1_out,
       not_2_out, or_1_out;
  wire [7:0] \四位二进制可逆计数器_1_qa ;
  wire [7:4] divider_1_out, divider_1_rem;

  or or_1 (or_1_out, CLR, comparator_2_eq);
  and and_1 (and_1_out, not_1_out, adj, CPD);
  not not_1 (not_1_out, comparator_1_eq);
  Comparator #(.width(8), .mode("twosComplement")) comparator_1 (
    .a(\四位二进制可逆计数器_1_qa ), .b({8{1'b0}}), .eq(comparator_1_eq));  // open: gt, lt
  and and_2 (and_2_out, \四位二进制可逆计数器_1_qa [0], \四位二进制可逆计数器_1_qa [1], \四位二进制可逆计数器_1_qa [2], \四位二进制可逆计数器_1_qa [3]);
  \四位二进制可逆计数器  \u_四位二进制可逆计数器_1  (
    .nLC(1'b1), .QD(\四位二进制可逆计数器_1_qa [3]), .QC(\四位二进制可逆计数器_1_qa [2]), .QB(\四位二进制可逆计数器_1_qa [1]),
    .QA(\四位二进制可逆计数器_1_qa [0]), .clr(or_1_out), .cpu(CPU), .cpd(and_1_out));  // open: D, C, B, A
  not not_2 (not_2_out, adj);
  and and_3 (and_3_out, and_2_out, CPU);
  nor nor_1 (nor_1_out, \四位二进制可逆计数器_1_qa [0], \四位二进制可逆计数器_1_qa [1], \四位二进制可逆计数器_1_qa [2], \四位二进制可逆计数器_1_qa [3]);
  and and_4 (and_4_out, nor_1_out, and_1_out);
  Comparator #(.width(8), .mode("twosComplement")) comparator_2 (
    .a(\四位二进制可逆计数器_1_qa ), .b(8'h3c), .eq(comparator_2_eq));  // open: gt, lt
  Divider #(.width(8)) divider_1 (
    .a(\四位二进制可逆计数器_1_qa ), .b(8'ha), .out({divider_1_out, Q1D, Q1C, Q1B, Q1A}),
    .rem({divider_1_rem, Q0D, Q0C, Q0B, Q0A}));  // open: upper
  \四位二进制可逆计数器  \u_四位二进制可逆计数器_2  (
    .nLC(1'b1), .QD(\四位二进制可逆计数器_1_qa [7]), .QC(\四位二进制可逆计数器_1_qa [6]), .QB(\四位二进制可逆计数器_1_qa [5]),
    .QA(\四位二进制可逆计数器_1_qa [4]), .clr(or_1_out), .cpu(and_3_out), .cpd(and_4_out));  // open: D, C, B, A
  nand nand_1 (nQCC, comparator_2_eq, not_2_out);
endmodule

module \十二进制或二十四进制计数器  (
  input  set,
  input  CPU,
  input  adj,
  input  CPD,
  input  CLR,
  output out_6,
  output out_7,
  output out_8,
  output out_9,
  output out_10,
  output out_11,
  output out_12,
  output out_13,
  output nQCC
);

  wire comparator_1_eq, comparator_2_eq, comparator_3_eq, comparator_4_gt, comparator_5_eq, comparator_6_eq,
       or_1_out, or_2_out, or_3_out;
  wire [7:0] multiplexer_1_out, multiplexer_2_out, multiplexer_3_out, subtractor_1_out, \六十进制计数器_1_q0a ;

  Comparator #(.width(8), .mode("twosComplement")) comparator_1 (
    .a(\六十进制计数器_1_q0a ), .b({8{1'b0}}), .eq(comparator_1_eq));  // open: gt, lt
  Comparator #(.width(8), .mode("twosComplement")) comparator_2 (
    .a(\六十进制计数器_1_q0a ), .b(8'h20), .eq(comparator_2_eq));  // open: gt, lt
  Comparator #(.width(8), .mode("twosComplement")) comparator_3 (
    .a(\六十进制计数器_1_q0a ), .b(8'h21), .eq(comparator_3_eq));  // open: gt, lt
  Multiplexer #(.select(1), .width(8), .disabled("Z"), .enable("false")) multiplexer_1 (
    .in0(\六十进制计数器_1_q0a ), .in1(8'h12), .out(multiplexer_1_out), .sel(comparator_1_eq));
  or or_1 (or_1_out, comparator_2_eq, comparator_3_eq);
  Multiplexer #(.select(1), .width(8), .disabled("Z"), .enable("false")) multiplexer_2 (
    .in0(8'h12), .in1(8'h18), .out(multiplexer_2_out), .sel(or_1_out));
  Comparator #(.width(8), .mode("twosComplement")) comparator_4 (
    .a(multiplexer_1_out), .b(8'h12), .gt(comparator_4_gt));  // open: eq, lt
  Subtractor #(.width(8)) subtractor_1 (
    .a(\六十进制计数器_1_q0a ), .b(multiplexer_2_out), .out(subtractor_1_out));  // open: bin, bout
  Multiplexer #(.select(1), .width(8), .disabled("Z"), .enable("false")) multiplexer_3 (
    .in0(multiplexer_1_out), .in1(subtractor_1_out), .out(multiplexer_3_out), .sel(comparator_4_gt));
  Multiplexer #(.select(1), .width(8), .disabled("Z"), .enable("false")) multiplexer_4 (
    .in0(multiplexer_3_out), .in1(\六十进制计数器_1_q0a ),
    .out({out_6, out_7, out_8, out_9, out_10, out_11, out_12, out_13}), .sel(set));
  \六十进制计数器  \u_六十进制计数器_1  (
    .adj(adj), .CPU(CPU), .CLR(or_2_out), .CPD(CPD), .Q1D(\六十进制计数器_1_q0a [7]), .Q1C(\六十进制计数器_1_q0a [6]),
    .Q1B(\六十进制计数器_1_q0a [5]), .Q1A(\六十进制计数器_1_q0a [4]), .Q0D(\六十进制计数器_1_q0a [3]), .Q0C(\六十进制计数器_1_q0a [2]),
    .Q0B(\六十进制计数器_1_q0a [1]), .Q0A(\六十进制计数器_1_q0a [0]));  // open: nQCC
  or or_2 (or_2_out, comparator_5_eq, CLR);
  Comparator #(.width(8), .mode("twosComplement")) comparator_5 (
    .a(\六十进制计数器_1_q0a ), .b(8'h24), .eq(comparator_5_eq));  // open: gt, lt
  Comparator #(.width(8), .mode("twosComplement")) comparator_6 (
    .a(\六十进制计数器_1_q0a ), .b(8'h12), .eq(comparator_6_eq));  // open: gt, lt
  or or_3 (or_3_out, comparator_5_eq, comparator_6_eq);
  not not_1 (nQCC, or_3_out);
endmodule

module \上午下午文字显示电路  (
  input  TT,
  input  AM_FM,
  output [4:0] out_3,
  output [4:0] out_4,
  output [4:0] out_5,
  output [4:0] out_6
);

  wire [4:0] multiplexer_2_out, multiplexer_4_out, multiplexer_6_out, multiplexer_8_out;

  Multiplexer #(.select(1), .width(5), .disabled("Z"), .enable("false")) multiplexer_1 (
    .in0({5{1'b0}}), .in1(multiplexer_2_out), .out(out_3), .sel(TT));
  Multiplexer #(.select(1), .width(5), .disabled("Z"), .enable("false")) multiplexer_2 (
    .in0(5'b00001), .in1(5'b10000), .out(multiplexer_2_out), .sel(AM_FM));
  Multiplexer #(.select(1), .width(5), .disabled("Z"), .enable("false")) multiplexer_3 (
    .in0({5{1'b0}}), .in1(multiplexer_4_out), .out(out_4), .sel(TT));
  Multiplexer #(.select(1), .width(5), .disabled("Z"), .enable("false")) multiplexer_4 (
    .in0({5{1'b1}}), .in1({5{1'b1}}), .out(multiplexer_4_out), .sel(AM_FM));
  Multiplexer #(.select(1), .width(5), .disabled("Z"), .enable("false")) multiplexer_5 (
    .in0({5{1'b0}}), .in1(multiplexer_6_out), .out(out_5), .sel(TT));
  Multiplexer #(.select(1), .width(5), .disabled("Z"), .enable("false")) multiplexer_6 (
    .in0(5'b00101), .in1(5'b10100), .out(multiplexer_6_out), .sel(AM_FM));
  Multiplexer #(.select(1), .width(5), .disabled("Z"), .enable("false")) multiplexer_7 (
    .in0({5{1'b0}}), .in1(multiplexer_8_out), .out(out_6), .sel(TT));
  Multiplexer #(.select(1), .width(5), .disabled("Z"), .enable("false")) multiplexer_8 (
    .in0(5'b00001), .in1(5'b10000), .out(multiplexer_8_out), .sel(AM_FM));
endmodule

module \六十进制计数器测试电路  (
  input  in_1,
  input  in_2,
  output out_3
);

  wire button_1_out, button_2_out;
  wire [3:0] \六十进制计数器_1_p7 , \六十进制计数器_1_p11 ;

  Button button_1 (.out(button_1_out));
  Button button_2 (.out(button_2_out));
  Hex_Digit_Display hex_digit_display_1 (.value(\六十进制计数器_1_p7 ));  // open: dp
  Hex_Digit_Display hex_digit_display_2 (.value(\六十进制计数器_1_p11 ));  // open: dp
  // 六十进制计数器 六十进制计数器_1: pin names not known; wires that end beside it: button_1_out, in_1, button_2_out, \六十进制计数器_1_p7 [3], \六十进制计数器_1_p7 [2], \六十进制计数器_1_p7 [1], \六十进制计数器_1_p7 [0], \六十进制计数器_1_p11 [3], \六十进制计数器_1_p11 [2], \六十进制计数器_1_p11 [1], \六十进制计数器_1_p11 [0], out_3, in_2
endmodule

module \十二进制或二十四进制测试电路  (
  input  adj,
  input  SET,
  input  CLR,
  input  adj_2,
  input  SET_2,
  input  adj_3,
  input  SET_3,
  input  CLR_2,
  input  CLR_3,
  output nQCC,
  output nQCC_2
);

  wire CPD_2_out, CPD_3_out, CPD_out, CPU_2_out, CPU_out, undriven;
  wire [3:0] \十二进制或二十四进制计数器_1_out_9 , \十二进制或二十四进制计数器_1_out_13 , \十二进制或二十四进制计数器_2_out_9 ,
       \十二进制或二十四进制计数器_2_out_13 , \十二进制或二十四进制计数器_3_out_9 , \十二进制或二十四进制计数器_3_out_13 ;

  Button CPU (.out(CPU_out));
  Button CPD (.out(CPD_out));
  Button CPU_2 (.out(CPU_2_out));
  Button CPD_2 (.out(CPD_2_out));
  Hex_Digit_Display hex_digit_display_1 (.value(\十二进制或二十四进制计数器_1_out_9 ));  // open: dp
  Hex_Digit_Display hex_digit_display_2 (.value(\十二进制或二十四进制计数器_2_out_9 ));  // open: dp
  Hex_Digit_Display hex_digit_display_3 (.value(\十二进制或二十四进制计数器_1_out_13 ));  // open: dp
  Hex_Digit_Display hex_digit_display_4 (.value(\十二进制或二十四进制计数器_2_out_13 ));  // open: dp
  \十二进制或二十四进制计数器  \u_十二进制或二十四进制计数器_1  (
    .out_6(\十二进制或二十四进制计数器_1_out_9 [3]), .out_7(\十二进制或二十四进制计数器_1_out_9 [2]),
    .out_8(\十二进制或二十四进制计数器_1_out_9 [1]), .out_9(\十二进制或二十四进制计数器_1_out_9 [0]),
    .out_10(\十二进制或二十四进制计数器_1_out_13 [3]), .out_11(\十二进制或二十四进制计数器_1_out_13 [2]),
    .out_12(\十二进制或二十四进制计数器_1_out_13 [1]), .out_13(\十二进制或二十四进制计数器_1_out_13 [0]), .set(SET), .CPU(CPU_out),
    .adj(adj), .CPD(CPD_out), .CLR(CLR));  // open: nQCC
  \十二进制或二十四进制计数器  \u_十二进制或二十四进制计数器_2  (
    .out_6(\十二进制或二十四进制计数器_2_out_9 [3]), .out_7(\十二进制或二十四进制计数器_2_out_9 [2]),
    .out_8(\十二进制或二十四进制计数器_2_out_9 [1]), .out_9(\十二进制或二十四进制计数器_2_out_9 [0]),
    .out_10(\十二进制或二十四进制计数器_2_out_13 [3]), .out_11(\十二进制或二十四进制计数器_2_out_13 [2]),
    .out_12(\十二进制或二十四进制计数器_2_out_13 [1]), .out_13(\十二进制或二十四进制计数器_2_out_13 [0]), .set(SET_2), .CPU(CPU_2_out),
    .adj(adj_2), .CPD(CPD_2_out), .CLR(CLR_2));  // open: nQCC
  Button CPD_3 (.out(CPD_3_out));
  Hex_Digit_Display hex_digit_display_5 (.value(\十二进制或二十四进制计数器_3_out_9 ));  // open: dp
  Hex_Digit_Display hex_digit_display_6 (.value(\十二进制或二十四进制计数器_3_out_13 ));  // open: dp
  \十二进制或二十四进制计数器  \u_十二进制或二十四进制计数器_3  (
    .out_6(\十二进制或二十四进制计数器_3_out_9 [3]), .out_7(\十二进制或二十四进制计数器_3_out_9 [2]),
    .out_8(\十二进制或二十四进制计数器_3_out_9 [1]), .out_9(\十二进制或二十四进制计数器_3_out_9 [0]),
    .out_10(\十二进制或二十四进制计数器_3_out_13 [3]), .out_11(\十二进制或二十四进制计数器_3_out_13 [2]),
    .out_12(\十二进制或二十四进制计数器_3_out_13 [1]), .out_13(\十二进制或二十四进制计数器_3_out_13 [0]), .set(SET_3), .CPU(undriven),
    .adj(adj_3), .CPD(CPD_3_out), .CLR(CLR_3));  // open: nQCC
endmodule

module \上午下午文字显示电路测试电路  (
  input  AM_FM,
  input  TT
);

  wire [4:0] \上午下午文字显示电路_1_out_3 , \上午下午文字显示电路_1_out_4 , \上午下午文字显示电路_1_out_5 , \上午下午文字显示电路_1_out_6 ;

  DotMatrix #(.inputtype("column"), .matrixcols(4), .matrixrows(5), .persist(0), .dotshape("square")) dotmatrix_1 (
    .col0(\上午下午文字显示电路_1_out_3 ), .col1(\上午下午文字显示电路_1_out_4 ), .col2(\上午下午文字显示电路_1_out_5 ),
    .col3(\上午下午文字显示电路_1_out_6 ));
  \上午下午文字显示电路  \u_上午下午文字显示电路_1  (
    .TT(TT), .AM_FM(AM_FM), .out_3(\上午下午文字显示电路_1_out_3 ), .out_4(\上午下午文字显示电路_1_out_4 ),
    .out_5(\上午下午文字显示电路_1_out_5 ), .out_6(\上午下午文字显示电路_1_out_6 ));
endmodule

module \电子钟整点报时电路  (
  input  [3:0] \分 ,
  input  [3:0] in_2,
  input  [3:0] \秒 ,
  input  [3:0] in_4,
  output out_5
);

  wire comparator_1_eq, comparator_2_eq, comparator_3_eq, comparator_4_gt;

  Comparator #(.width(4), .mode("unsigned")) comparator_1 (.a(4'b0101), .b(\分 ), .eq(comparator_1_eq));  // open: gt, lt
  Comparator #(.width(4), .mode("unsigned")) comparator_2 (
    .a(4'b1001), .b(in_2), .eq(comparator_2_eq));  // open: gt, lt
  Comparator #(.width(4), .mode("unsigned")) comparator_3 (.a(4'b0101), .b(\秒 ), .eq(comparator_3_eq));  // open: gt, lt
  Comparator #(.width(4), .mode("unsigned")) comparator_4 (
    .a(4'b1010), .b(in_4), .gt(comparator_4_gt));  // open: eq, lt
  and and_1 (out_5, comparator_1_eq, comparator_2_eq, comparator_3_eq, comparator_4_gt);
endmodule

module \电子钟整点报时测试电路  (
  input  [3:0] in_1,
  input  [3:0] in_2,
  input  [3:0] in_3,
  input  [3:0] in_4
);

  wire \电子钟整点报时电路_1_out_5 ;

  LED #(.active("true")) led_1 (.in(\电子钟整点报时电路_1_out_5 ));
  \电子钟整点报时电路  \u_电子钟整点报时电路_1  (.\分 (in_1), .in_2(in_2), .\秒 (in_3), .in_4(in_4), .out_5(\电子钟整点报时电路_1_out_5 ));
endmodule

module \多功能数字钟  (
  input  SET,
  input  CLR,
  input  Adj0,
  input  Adj1,
  input  CPU,
  input  CPD,
  input  CP,
  output [3:0] out_8,
  output [3:0] out_9,
  output [4:0] out_10,
  output [4:0] out_11,
  output [4:0] out_12,
  output [4:0] out_13,
  output [3:0] out_14,
  output [3:0] out_15,
  output [3:0] out_16,
  output [3:0] out_17,
  output out_18
);

  wire and_1_out, and_2_out, and_3_out, and_4_out, and_5_out, and_6_out, not_1_out, not_2_out, not_3_out,
       not_4_out, not_5_out, or_1_out, or_2_out, t_ff_1_q, undriven, \六十进制计数器_1_nqcc , \六十进制计数器_2_nqcc ,
       \秒脉冲产生电路_1_out_2 ;

  not not_1 (not_1_out, undriven);
  \十二进制或二十四进制计数器  \u_十二进制或二十四进制计数器_1  (
    .out_6(out_8[3]), .out_7(out_8[2]), .out_8(out_8[1]), .out_9(out_8[0]), .out_10(out_9[3]),
    .out_11(out_9[2]), .out_12(out_9[1]), .out_13(out_9[0]), .set(SET), .CPU(or_1_out), .adj(Adj0),
    .CPD(and_1_out), .CLR(CLR));  // open: nQCC
  and and_1 (and_1_out, and_4_out, not_3_out);
  \秒脉冲产生电路  \u_秒脉冲产生电路_1  (.out_2(\秒脉冲产生电路_1_out_2 ), .in_1(CP));
  \上午下午文字显示电路  \u_上午下午文字显示电路_1  (
    .TT(not_2_out), .AM_FM(t_ff_1_q), .out_3(out_10), .out_4(out_11), .out_5(out_12), .out_6(out_13));
  not not_2 (not_2_out, SET);
  T_Flip_Flop #(.trigger("rising"), .Pre_Clr_Positions("LEGACY"), .NegatePresetClear("false"), .enable("true"), .NewFFLayout("false")) t_ff_1 (
    .clk(not_1_out), .T(1'b1), .Q(t_ff_1_q));  // open: Qn, preset, reset, en
  or or_1 (or_1_out, not_4_out, and_3_out);
  and and_2 (and_2_out, Adj1, and_4_out);
  and and_3 (and_3_out, not_3_out, and_5_out);
  and and_4 (and_4_out, CPD, Adj0);
  not not_3 (not_3_out, Adj1);
  not not_4 (not_4_out, \六十进制计数器_1_nqcc );
  \六十进制计数器  \u_六十进制计数器_1  (
    .adj(Adj0), .CPU(or_2_out), .CLR(CLR), .CPD(and_2_out), .Q1D(out_14[3]), .Q1C(out_14[2]),
    .Q1B(out_14[1]), .Q1A(out_14[0]), .Q0D(out_15[3]), .Q0C(out_15[2]), .Q0B(out_15[1]), .Q0A(out_15[0]),
    .nQCC(\六十进制计数器_1_nqcc ));
  and and_5 (and_5_out, CPU, Adj0);
  or or_2 (or_2_out, not_5_out, and_6_out);
  and and_6 (and_6_out, Adj1, and_5_out);
  \六十进制计数器  \u_六十进制计数器_2  (
    .adj(Adj0), .CPU(\秒脉冲产生电路_1_out_2 ), .CLR(CLR), .Q1D(out_16[3]), .Q1C(out_16[2]), .Q1B(out_16[1]),
    .Q1A(out_16[0]), .Q0D(out_17[3]), .Q0C(out_17[2]), .Q0B(out_17[1]), .Q0A(out_17[0]),
    .nQCC(\六十进制计数器_2_nqcc ));  // open: CPD
  not not_5 (not_5_out, \六十进制计数器_2_nqcc );
  \电子钟整点报时电路  \u_电子钟整点报时电路_1  (.\分 (out_14), .in_2(out_15), .\秒 (out_16), .in_4(out_17), .out_5(out_18));
endmodule

module \秒脉冲产生电路  (
  input  in_1,
  output out_2
);

  Counter #(.width(8), .max('h7), .ongoal("wrap"), .trigger("falling"), .behavior("old")) counter_1 (
    .count(1'b1), .carry(out_2), .clk(in_1));  // open: load, D, Q, clr, preset
endmodule

module \多动能数字钟测试电路  (
  input  in_1,
  input  in_2,
  input  in_3,
  input  in_4
);

  wire button_1_out, button_2_out, clock_1_out, \多功能数字钟_1_out_18 ;
  wire [3:0] \多功能数字钟_1_out_8 , \多功能数字钟_1_out_9 , \多功能数字钟_1_out_14 , \多功能数字钟_1_out_15 , \多功能数字钟_1_out_16 ,
       \多功能数字钟_1_out_17 ;
  wire [4:0] \多功能数字钟_1_out_10 , \多功能数字钟_1_out_11 , \多功能数字钟_1_out_12 , \多功能数字钟_1_out_13 ;

  DotMatrix #(.inputtype("column"), .matrixcols(4), .matrixrows(5), .persist(0), .dotshape("square")) dotmatrix_1 (
    .col0(\多功能数字钟_1_out_10 ), .col1(\多功能数字钟_1_out_11 ), .col2(\多功能数字钟_1_out_12 ), .col3(\多功能数字钟_1_out_13 ));
  Clock #(.highDuration(1), .lowDuration(1)) clock_1 (.out(clock_1_out));
  Hex_Digit_Display hex_digit_display_1 (.value(\多功能数字钟_1_out_8 ));  // open: dp
  Hex_Digit_Display hex_digit_display_2 (.value(\多功能数字钟_1_out_9 ));  // open: dp
  Button button_1 (.out(button_1_out));
  Hex_Digit_Display hex_digit_display_3 (.value(\多功能数字钟_1_out_15 ));  // open: dp
  Hex_Digit_Display hex_digit_display_4 (.value(\多功能数字钟_1_out_14 ));  // open: dp
  Button button_2 (.out(button_2_out));
  Hex_Digit_Display hex_digit_display_5 (.value(\多功能数字钟_1_out_16 ));  // open: dp
  Hex_Digit_Display hex_digit_display_6 (.value(\多功能数字钟_1_out_17 ));  // open: dp
  \多功能数字钟  \u_多功能数字钟_1  (
    .SET(in_3), .CLR(in_4), .Adj0(in_1), .Adj1(in_2), .CPU(button_1_out), .CPD(button_2_out),
    .CP(clock_1_out), .out_18(\多功能数字钟_1_out_18 ), .out_8(\多功能数字钟_1_out_8 ), .out_9(\多功能数字钟_1_out_9 ),
    .out_10(\多功能数字钟_1_out_10 ), .out_11(\多功能数字钟_1_out_11 ), .out_12(\多功能数字钟_1_out_12 ),
    .out_13(\多功能数字钟_1_out_13 ), .out_14(\多功能数字钟_1_out_14 ), .out_15(\多功能数字钟_1_out_15 ),
    .out_16(\多功能数字钟_1_out_16 ), .out_17(\多功能数字钟_1_out_17 ));
  LED #(.active("true")) led_1 (.in(\多功能数字钟_1_out_18 ));
endmodule
